// Digital circuit diglab_2023_final_01.dig as structural Verilog
module diglab_2023_final_01 (
  input  reset,
  input  clk,
  output A,
  output B,
  output C
);

  wire and_1_out, and_2_out, and_3_out, and_4_out, and_5_out, and_6_out, and_7_out, and_8_out, not_1_out,
       not_2_out, not_3_out, not_4_out, or_1_out, or_2_out, or_3_out;

  not not_1 (not_1_out, reset);
  not not_2 (not_2_out, C);
  not not_3 (not_3_out, B);
  not not_4 (not_4_out, A);
  and and_1 (and_1_out, A, not_3_out, C, not_1_out);
  and and_2 (and_2_out, not_4_out, B, not_1_out);
  and and_3 (and_3_out, B, not_2_out, not_1_out);
  and and_4 (and_4_out, A, not_2_out, not_1_out);
  and and_5 (and_5_out, A, not_3_out, not_1_out);
  and and_6 (and_6_out, not_3_out, not_2_out, not_1_out);
  and and_7 (and_7_out, A, not_3_out, not_1_out);
  and and_8 (and_8_out, not_4_out, C, not_1_out);
  or or_1 (or_1_out, and_1_out, and_2_out, and_3_out);
  or or_2 (or_2_out, and_4_out, and_5_out, and_6_out);
  or or_3 (or_3_out, and_7_out, and_8_out);
  D_FF Z_2_n (.D(or_1_out), .C(clk), .Q(C));  // open: nQ
  D_FF Z_1_n (.D(or_2_out), .C(clk), .Q(B));  // open: nQ
  D_FF Z_0_n (.D(or_3_out), .C(clk), .Q(A));  // open: nQ

  // Other names for the same wires on the sheet: Z_0_n = A; Z_1_n = B; Z_2_n = C
endmodule

/* Test case TestCase:
clk reset C B A
0 0 0 0 0 
0 1 0 0 0
1 1 0 0 0
0 0 0 0 0
1 0 0 1 0
0 0 0 1 0
1 0 1 0 0
0 0 1 0 0 
1 0 0 0 1
0 0 0 0 1
1 0 0 1 1
0 0 0 1 1
1 0 1 1 0
0 0 1 1 0
1 0 1 0 1
0 0 1 0 1
1 0 1 1 1
0 0 1 1 1
1 0 0 0 0
0 0 0 0 0
1 0 0 1 0
0 0 0 1 0
1 0 1 0 0
0 0 1 0 0 
1 0 0 0 1
0 0 0 0 1
1 0 0 1 1
0 0 0 1 1
1 0 1 1 0
0 0 1 1 0
1 0 1 0 1
0 0 1 0 1
1 0 1 1 1
0 0 1 1 1
*/
