// Digital circuit diglab_2023_final_02.dig as structural Verilog
module diglab_2023_final_02 (
  input  [15:0] A,
  input  \input ,
  input  clk,
  output busy,
  output [7:0] ed,
  output [7:0] sqrt,
  output [7:0] st
);

  wire comparator_1_gt, comparator_3_eq, comparator_3_gt, comparator_3_lt, or_1_out, or_2_out;
  wire [0:0] add_1_s;
  wire [7:0] md, multiplexer_2_out;
  wire [15:0] A_t, multiplexer_1_out, square;

  Comparator #(.Bits(16)) comparator_1 (.a(A), .b({16{1'b0}}), .gt(comparator_1_gt));  // open: eq, lt
  Mul #(.Bits(8)) mul_1 (.a(md), .b(md), .mul(square));
  Add #(.Bits(8)) add_1 (.a(sqrt), .b(ed), .c_i(1'b0), .s({md[6:0], add_1_s[0]}), .c_o(md[7]));
  Comparator #(.Bits(8)) comparator_2 (.a(md), .b(sqrt), .gt(busy));  // open: eq, lt
  Multiplexer #(.Bits(16)) multiplexer_1 (.sel(comparator_1_gt), .in_0(A_t), .in_1(A), .out(multiplexer_1_out));
  Register #(.Bits(16)) register_1 (.D(multiplexer_1_out), .C(clk), .en(comparator_1_gt), .Q(A_t));
  Comparator #(.Bits(16)) comparator_3 (
    .a(square), .b(A_t), .gt(comparator_3_gt), .eq(comparator_3_eq), .lt(comparator_3_lt));
  or or_1 (or_1_out, comparator_3_eq, comparator_3_lt);
  Multiplexer #(.Bits(8)) multiplexer_2 (.sel(\input ), .in_0(md), .in_1({8{1'b1}}), .out(multiplexer_2_out));
  or or_2 (or_2_out, \input , comparator_3_gt);
  Register #(.Bits(8)) register_2 (.D(md), .C(clk), .en(or_1_out), .Q(sqrt));
  Register #(.Bits(8)) register_3 (.D(multiplexer_2_out), .C(clk), .en(or_2_out), .Q(ed));

  assign st = sqrt;
endmodule

/* Test case TestCase1:
clk A input sqrt busy
0 0 0 0 0
1 0 0 0 0
0 0 0 0 0
1 0 0 0 0
0 0 1 X X
1 0 1 X X
repeat (80) C 0 0 X X
0 0 0 0 0
1 0 0 0 0
*/

/* Test case TestCase2:
clk A input sqrt busy
0 0 0 0 0
1 0 0 0 0
0 0 0 0 0
1 0 0 0 0
0 1 1 X X
1 1 1 X X
repeat (80) C 1 0 X X
0 0 0 1 0
1 0 0 1 0
*/

/* Test case TestCase3:
clk A input sqrt busy
0 0 0 0 0
1 0 0 0 0
0 0 0 0 0
1 0 0 0 0
0 4 1 X X
1 4 1 X X
repeat (80) C 4 0 X X
0 0 0 2 0
1 0 0 2 0
*/

/* Test case TestCase4:
clk A input sqrt busy
0 0 0 0 0
1 0 0 0 0
0 0 0 0 0
1 0 0 0 0
0 9 1 X X
1 9 1 X X
repeat (80) C 9 0 X X
0 0 0 3 0
1 0 0 3 0
*/

/* Test case TestCase5:
clk A input sqrt busy
0 0 0 0 0
1 0 0 0 0
0 0 0 0 0
1 0 0 0 0
0 8 1 X X
1 8 1 X X
repeat (80) C 8 0 X X
0 0 0 2 0
1 0 0 2 0
*/
