// Digital circuit diglab_2023_final_03.dig as structural Verilog
module diglab_2023_final_03 (
  input  [15:0] A,
  input  \input ,
  input  clk,
  input  reset,
  output [15:0] second
);

  wire and_1_out, and_2_out, and_3_out, equal1, equal2, greater1, greater2, lesser1, lesser2, or_1_out,
       or_2_out, or_3_out;
  wire [15:0] first, multiplexer_1_out;

  and and_1 (and_1_out, lesser1, greater2);
  Comparator #(.Bits(16)) comparator_1 (.a(A), .b(first), .gt(greater1), .eq(equal1), .lt(lesser1));
  Comparator #(.Bits(16)) comparator_2 (.a(A), .b(second), .gt(greater2), .eq(equal2), .lt(lesser2));
  or or_1 (or_1_out, equal1, greater1);
  or or_2 (or_2_out, equal1, greater1);
  or or_3 (or_3_out, equal1, greater1, 1'b0, and_1_out);
  and and_2 (and_2_out, \input , or_1_out);
  and and_3 (and_3_out, \input , or_3_out);
  Multiplexer #(.Bits(16)) multiplexer_1 (.sel(or_2_out), .in_0(A), .in_1(first), .out(multiplexer_1_out));
  Register #(.Bits(16)) register_1 (.D(A), .C(clk), .en(and_2_out), .Q(first));
  Register #(.Bits(16)) register_2 (.D(multiplexer_1_out), .C(clk), .en(and_3_out), .Q(second));

  // Notes on the sheet:
  //   clk: Hz: 200
endmodule

/* Test case Case1:
clk A input reset second
0 0 0 0 0
1 0 0 0 0
0 0 0 1 0
1 0 0 1 0
0 0  0 0 0
1 0  0 0 0
0 5 1 0 X
1 5 1 0 X
0  0 0 0 0
1  0 0 0 0
0 12 1 0 X
1 12 1 0 X
0  0 0 0 X
1  0 0 0 5
*/

/* Test case Case2:
clk A input reset second
0 0 0 0 0
1 0 0 0 0
0 0 0 1 0
1 0 0 1 0
0 0  0 0 0
1 0  0 0 0
0 5 1 0 X
1 5 1 0 X
0  0 0 0 0
1  0 0 0 0
0 15 1 0 X
1 15 1 0 X
0  0 0 0 X
1  0 0 0 5
*/

/* Test case Case3:
clk A input reset second
0 0 0 0 0
1 0 0 0 0
0 0 0 1 0
1 0 0 1 0
0 0  0 0 0
1 0  0 0 0
0 65535 1 0 X
1 65535 1 0 X
0  0 0 0 0
1  0 0 0 0
0 65524 1 0 X
1 65524 1 0 X
0  0 0 0 X
1  0 0 0 65524
*/
