// Digital circuit 10.dig as structural Verilog
module _10 (
  input  [8:0] N,
  input  reset,
  input  start,
  input  clock,
  output done,
  output [7:0] displayout,
  output [15:0] clockcount,
  output valid
);

  wire comparator_1_lt, comparator_2_gt, comparator_3_gt, multiplexer_10_out, multiplexer_11_out,
       multiplexer_14_out, not_1_out, or_1_out, s0, s1, s2, s3, s4, s5, s6, s7;
  wire [2:0] multiplexer_2_out, multiplexer_3_out, state, state_q, stateFrom0, stateFrom1, stateFrom4,
       stateFrom5;
  wire [7:0] multiplexer_9_out, ROMout;
  wire [8:0] add_1_s, add_2_s, add_4_s, count, index, multiplexer_8_out, multiplexer_12_out,
       multiplexer_13_out, multiplexer_16_out, RAMout, sub_1_s, temp;
  wire [15:0] add_3_s, multiplexer_15_out;

  Comparator #(.Bits(9)) comparator_1 (.a(index), .b(N), .lt(comparator_1_lt));  // open: gt, eq
  Multiplexer #(.Selector_Bits(3), .Bits(3)) multiplexer_1 (
    .sel(state_q), .in_0(stateFrom0), .in_1(stateFrom1), .in_2(3'b001), .in_3(3'b100), .in_4(stateFrom4),
    .in_5(stateFrom5), .in_6(3'b101), .in_7(3'b111), .out(state));
  D_FF #(.Bits(3)) u_state (.D(state), .C(clock), .Q(state_q));  // open: nQ
  Multiplexer #(.Bits(3)) multiplexer_2 (.sel(not_1_out), .in_0(3'b010), .in_1(3'b011), .out(multiplexer_2_out));
  not not_1 (not_1_out, comparator_1_lt);
  Multiplexer #(.Bits(3)) multiplexer_3 (.sel(reset), .in_0(3'b101), .in_1(3'b000), .out(multiplexer_3_out));
  Comparator #(.Bits(9)) comparator_2 (.a(index), .b(9'hff), .gt(comparator_2_gt));  // open: eq, lt
  Comparator #(.Bits(9)) comparator_3 (.a(count), .b({9{1'b0}}), .gt(comparator_3_gt));  // open: eq, lt
  Multiplexer #(.Bits(3)) multiplexer_4 (.sel(start), .in_0(3'b000), .in_1(3'b001), .out(stateFrom0));
  Multiplexer #(.Bits(3)) multiplexer_5 (.sel(reset), .in_0(multiplexer_2_out), .in_1(3'b000), .out(stateFrom1));
  Multiplexer #(.Bits(3)) multiplexer_6 (
    .sel(comparator_2_gt), .in_0(multiplexer_3_out), .in_1(3'b111), .out(stateFrom4));
  Multiplexer #(.Bits(3)) multiplexer_7 (.sel(comparator_3_gt), .in_0(3'b100), .in_1(3'b110), .out(stateFrom5));
  Decoder #(.Selector_Bits(3)) decoder_1 (
    .sel(state), .out_0(s0), .out_1(s1), .out_2(s2), .out_3(s3), .out_4(s4), .out_5(s5), .out_6(s6),
    .out_7(s7));
  Add #(.Bits(9)) add_1 (.a(index), .b({9{1'b0}}), .c_i(1'b1), .s(add_1_s));  // open: c_o
  Sub #(.Bits(9)) sub_1 (.a(count), .b(9'h1), .c_i(1'b0), .s(sub_1_s));  // open: c_o
  Multiplexer #(.Selector_Bits(3), .Bits(9)) multiplexer_8 (
    .sel(state), .in_0({9{1'b0}}), .in_1(index), .in_2(add_1_s), .in_3({9{1'b1}}), .in_4(add_1_s),
    .in_5(index), .in_6(index), .in_7(index), .out(multiplexer_8_out));
  Multiplexer #(.Selector_Bits(3), .Bits(8)) multiplexer_9 (
    .sel(state), .in_0({8{1'b0}}), .in_1(displayout), .in_2(displayout), .in_3(displayout),
    .in_4(displayout), .in_5(displayout), .in_6(index[7:0]), .in_7(displayout), .out(multiplexer_9_out));
  Multiplexer #(.Selector_Bits(3)) multiplexer_10 (
    .sel(state), .in_0(1'b0), .in_1(1'b0), .in_2(1'b0), .in_3(1'b0), .in_4(1'b0), .in_5(1'b0), .in_6(1'b1),
    .in_7(1'b0), .out(multiplexer_10_out));
  Multiplexer #(.Selector_Bits(3)) multiplexer_11 (
    .sel(state), .in_0(1'b0), .in_1(done), .in_2(done), .in_3(done), .in_4(done), .in_5(done), .in_6(done),
    .in_7(1'b1), .out(multiplexer_11_out));
  Multiplexer #(.Bits(9)) multiplexer_12 (.sel(or_1_out), .in_0(temp), .in_1(RAMout), .out(multiplexer_12_out));
  Multiplexer #(.Selector_Bits(3), .Bits(9)) multiplexer_13 (
    .sel(state), .in_0({9{1'b0}}), .in_1(count), .in_2(count), .in_3(count), .in_4(RAMout), .in_5(count),
    .in_6(sub_1_s), .in_7(count), .out(multiplexer_13_out));
  D_FF #(.Bits(9)) u_index (.D(multiplexer_8_out), .C(clock), .Q(index));  // open: nQ
  D_FF #(.Bits(8)) u_displayout (.D(multiplexer_9_out), .C(clock), .Q(displayout));  // open: nQ
  D_FF u_valid (.D(multiplexer_10_out), .C(clock), .Q(valid));  // open: nQ
  D_FF u_done (.D(multiplexer_11_out), .C(clock), .Q(done));  // open: nQ
  D_FF #(.Bits(9)) u_temp (.D(multiplexer_12_out), .C(clock), .Q(temp));  // open: nQ
  D_FF #(.Bits(9)) u_count (.D(multiplexer_13_out), .C(clock), .Q(count));  // open: nQ
  Multiplexer multiplexer_14 (.sel(done), .in_0(start), .in_1(1'b0), .out(multiplexer_14_out));
  Add #(.Bits(9)) add_2 (.a(index), .b({9{1'b0}}), .c_i(1'b1), .s(add_2_s));  // open: c_o
  Seven_Seg_Hex seven_seg_hex_1 (.d(displayout[7:4]), .dp(1'b0));
  Multiplexer #(.Bits(16)) multiplexer_15 (.sel(reset), .in_0(clockcount), .in_1({16{1'b0}}), .out(multiplexer_15_out));
  Seven_Seg_Hex seven_seg_hex_2 (.d(displayout[3:0]), .dp(1'b0));
  Add #(.Bits(16)) add_3 (.a(multiplexer_15_out), .b({16{1'b0}}), .c_i(multiplexer_14_out), .s(add_3_s));  // open: c_o
  Multiplexer #(.Bits(9)) multiplexer_16 (.sel(s4), .in_0({1'b0, ROMout}), .in_1(add_2_s), .out(multiplexer_16_out));
  Add #(.Bits(9)) add_4 (.a(temp), .b({9{1'b0}}), .c_i(1'b1), .s(add_4_s));  // open: c_o
  or or_1 (or_1_out, s1, s4);
  D_FF #(.Bits(16)) d_ff_1 (.D(add_3_s), .C(clock), .Q(clockcount));  // open: nQ
  ROM #(.AddrBits(9), .isProgramMemory("true"), .Bits(8)) ROMFILE (.A(index), .sel(1'b1), .D(ROMout));
  RAMDualPort #(.AddrBits(9), .Bits(9)) RAM (
    .A(multiplexer_16_out), .Din(add_4_s), .str(s2), .C(clock), .ld(or_1_out), .D(RAMout));

  // Notes on the sheet:
  //   contents of ROMFILE (hex, n*v repeats v):
  //   4,3,1,2
endmodule

/* Test case FINALT1:
clock N reset start valid displayout done clockcount
            program(0,0,1,1,2,2,3,3,4,4,5,5,6,6,7,7,8,8,9,9,10,10,11,11,12,12,13,13,14,14,15,15,16,16,17,17,18,18,19,19,20,20,21,21,22,22,23,23,24,24,25,25,26,26,27,27,28,28,29,29,30,30,31,31,32,32,33,33,34,34,35,35,36,36,37,37,38,38,39,39,40,40,41,41,42,42,43,43,44,44,45,45,46,46,47,47,48,48,49,49,50,50,51,51,52,52,53,53,54,54,55,55,56,56,57,57,58,58,59,59,60,60,61,61,62,62,63,63,64,64,65,65,66,66,67,67,68,68,69,69,70,70,71,71,72,72,73,73,74,74,75,75,76,76,77,77,78,78,79,79,80,80,81,81,82,82,83,83,84,84,85,85,86,86,87,87,88,88,89,89,90,90,91,91,92,92,93,93,94,94,95,95,96,96,97,97,98,98,99,99,100,100,101,101,102,102,103,103,104,104,105,105,106,106,107,107,108,108,109,109,110,110,111,111,112,112,113,113,114,114,115,115,116,116,117,117,118,118,119,119,120,120,121,121,122,122,123,123,124,124,125,125,126,126,127,127,128,128,129,129,130,130,131,131,132,132,133,133,134,134,135,135,136,136,137,137,138,138,139,139,140,140,141,141,142,142,143,143,144,144,145,145,146,146,147,147,148,148,149,149,150,150,151,151,152,152,153,153,154,154,155,155,156,156,157,157,158,158,159,159,160,160,161,161,162,162,163,163,164,164,165,165,166,166,167,167,168,168,169,169,170,170,171,171,172,172,173,173,174,174,175,175,176,176,177,177,178,178,179,179,180,180,181,181,182,182,183,183,184,184,185,185,186,186,187,187,188,188,189,189,190,190,191,191,192,192,193,193,194,194,195,195,196,196,197,197,198,198,199,199,200,200,201,201,202,202,203,203,204,204,205,205,206,206,207,207,208,208,209,209,210,210,211,211,212,212,213,213,214,214,215,215,216,216,217,217,218,218,219,219,220,220,221,221,222,222,223,223,224,224,225,225,226,226,227,227,228,228,229,229,230,230,231,231,232,232,233,233,234,234,235,235,236,236,237,237,238,238,239,239,240,240,241,241,242,242,243,243,244,244,245,245,246,246,247,247,248,248,249,249,250,250,251,251,252,252,253,253,254,254,255,255)
0 512 0 0 X X X X
1 512 0 0 X X X X
0 512 1 0 X X X X
1 512 1 0 X X X X
0 512 0 1 X X X X
1 512 0 1 X X X X
repeat (40000) C 512 0 1 X X X X
1 512 0 1 X X X 0xBAADBEEF
*/
