// Digital circuit H-C.dig as structural Verilog
module H_C (
  input  [6:0] P,
  input  [6:0] H,
  output [6:0] O
);

  xor xor_1 (O[6], P[6], H[6]);
  xor xor_2 (O[5], P[5], H[5]);
  xor xor_3 (O[4], P[4], H[4]);
  xor xor_4 (O[3], P[3], H[3]);
  xor xor_5 (O[2], P[2], H[2]);
  xor xor_6 (O[1], P[1], H[1]);
  xor xor_7 (O[0], P[0], H[0]);
endmodule
