// Digital circuit 642-3.dig as structural Verilog
module _642_3 (
  input  A,
  input  B,
  input  C,
  input  D,
  output [3:0] O
);

  wire and_1_out, and_2_out, and_3_out, and_4_out, and_5_out, and_6_out, and_7_out, not_1_out, not_2_out,
       not_3_out, not_4_out;

  not not_1 (not_1_out, A);
  not not_2 (not_2_out, B);
  not not_3 (not_3_out, C);
  not not_4 (not_4_out, D);
  and and_1 (and_1_out, B, D);
  and and_2 (and_2_out, C, D);
  and and_3 (and_3_out, B, not_4_out);
  and and_4 (and_4_out, B, C);
  and and_5 (and_5_out, not_2_out, not_3_out, D);
  and and_6 (and_6_out, C, not_4_out);
  and and_7 (and_7_out, B, not_3_out, D);
  or or_1 (O[3], A, and_1_out, and_2_out);
  or or_2 (O[2], and_3_out, and_4_out, and_5_out);
  or or_3 (O[1], A, and_6_out, and_7_out);

  assign O[0] = D;
endmodule
