// Digital circuit 02.dig as structural Verilog
module _02 (
  input  [6:0] In,
  output [6:0] Output
);

  wire a_part_circuit_1_c1, a_part_circuit_1_c2, a_part_circuit_1_c3, b_part_circuit_1_w1,
       b_part_circuit_1_w2, b_part_circuit_1_w3, b_part_circuit_1_w4, b_part_circuit_1_w5,
       b_part_circuit_1_w6, b_part_circuit_1_w7;

  A_part_circuit a_part_circuit_1 (
    .I1(In[0]), .I2(In[1]), .I3(In[2]), .I4(In[3]), .I5(In[4]), .I6(In[5]), .I7(In[6]),
    .C1(a_part_circuit_1_c1), .C2(a_part_circuit_1_c2), .C3(a_part_circuit_1_c3));
  B_part_circuit b_part_circuit_1 (
    .C1(a_part_circuit_1_c1), .C2(a_part_circuit_1_c2), .C3(a_part_circuit_1_c3), .W1(b_part_circuit_1_w1),
    .W2(b_part_circuit_1_w2), .W3(b_part_circuit_1_w3), .W4(b_part_circuit_1_w4), .W5(b_part_circuit_1_w5),
    .W6(b_part_circuit_1_w6), .W7(b_part_circuit_1_w7));
  // C_part_circuit c_part_circuit_1: pin names not known; wires that end beside it: In[0], b_part_circuit_1_w1, In[1], b_part_circuit_1_w2, In[2], b_part_circuit_1_w3, In[3], b_part_circuit_1_w4, In[4], b_part_circuit_1_w5, In[5], b_part_circuit_1_w6, In[6], b_part_circuit_1_w7, Output[0], Output[1], Output[2], Output[3], Output[4], Output[5], Output[6]
endmodule
