// Digital circuit B-part-circuit.dig as structural Verilog
module B_part_circuit (
  input  C1,
  input  C2,
  input  C3,
  output W1,
  output W2,
  output W3,
  output W4,
  output W5,
  output W6,
  output W7
);

  and and_1 (W1, C3, ~C2, ~C1);  // And
  and and_2 (W2, ~C3, C2, ~C1);  // And
  and and_3 (W3, C3, C2, ~C1);  // And
  and and_4 (W4, ~C3, ~C2, C1);  // And
  and and_5 (W5, C3, ~C2, C1);  // And
  and and_6 (W6, ~C3, C2, C1);  // And
  and and_7 (W7, C3, C2, C1);
endmodule
