// Digital circuit 04.dig as structural Verilog
module _04 (
  input  [3:0] In,
  output [3:0] Output
);

  wire or_1_out;
  wire [2:0] sub_1_s;

  or or_1 (or_1_out, In[0], In[1], In[2]);
  Sub #(.Bits(3)) sub_1 (.a(3'b000), .b(In[2:0]), .c_i(1'b0), .s(sub_1_s));  // open: c_o
  Multiplexer #(.Bits(3)) multiplexer_1 (.sel(In[3]), .in_0(In[2:0]), .in_1(sub_1_s), .out(Output[2:0]));
  Multiplexer multiplexer_2 (.sel(In[3]), .in_0(1'b0), .in_1(or_1_out), .out(Output[3]));
endmodule
