// Digital circuit 05_wrong.dig as structural Verilog
module _05_wrong (
  input  T,
  input  Clear,
  input  Clock,
  output Q,
  output Q_2
);

  wire nor_1_out, nor_2_out, not_1_out;

  not not_1 (not_1_out, Clock);
  nor nor_1 (nor_1_out, T, not_1_out);
  nor nor_2 (nor_2_out, not_1_out, T);
  nor nor_3 (Q, nor_1_out, Q_2);
  nor nor_4 (Q_2, Q, nor_2_out);
endmodule
