// Digital circuit Template.dig as structural Verilog
module Template (
  input  T,
  input  Clear,
  input  Clock,
  output Q,
  output Q_2
);

  wire and_1_out, and_2_out, not_1_out;

  not not_1 (not_1_out, Clock);
  and and_1 (and_1_out, Q, T, not_1_out);
  and and_2 (and_2_out, not_1_out, T, Q_2);
  nor nor_1 (Q, and_1_out, Clear, Q_2);
  nor nor_2 (Q_2, Q, and_2_out);
endmodule
