// Digital circuit 09.dig as structural Verilog
module _09 (
  input  P5,
  input  reset,
  input  clock,
  input  P10,
  input  P20,
  input  Pcoffee,
  input  Ptea,
  input  Pchange,
  input  Pnext,
  input  clock_2,
  output [5:0] Balance,
  output CoffeeOut,
  output TeaOut,
  output [1:0] Change5,
  output [1:0] Change10,
  output [1:0] Change20,
  output [3:0] State
);

  wire and_1_out, and_2_out, and_3_out, and_4_out, and_5_out, and_6_out, and_7_out, and_8_out, and_9_out,
       and_10_out, and_11_out, and_12_out, comparator_1_eq, comparator_9_gt, comparator_10_gt,
       comparator_11_gt, comparator_12_lt, comparator_13_lt, d_ff_7_nq, d_ff_8_nq, d_ff_9_nq, d_ff_10_nq,
       d_ff_15_nq, d_ff_16_nq, d_ff_17_nq, nor_1_out, not_1_out, not_2_out, not_3_out, not_4_out, not_5_out,
       P5_t, P10_t, P20_t, PChange_t, Pchange_t_t, PCoffee_t, Pcoffee_t_t, Pnext_t, PTea_t, Ptea_t_t;
  wire [3:0] multiplexer_1_out, multiplexer_2_out, nextStateFrom0001;
  wire [5:0] add_1_s, add_2_s, add_3_s, multiplexer_3_out, sub_1_s, sub_2_s;

  D_FF #(.Bits(4)) d_ff_1 (.D(multiplexer_1_out), .C(clock), .Q(State));  // open: nQ
  Multiplexer #(.Bits(4), .Selector_Bits(4)) multiplexer_1 (
    .sel(State), .in_0(4'b0001), .in_1(nextStateFrom0001), .in_2(4'b0001), .in_3(4'b0001), .in_4(4'b0111),
    .in_5(4'b0111), .in_6(4'b0000), .in_7(4'b0000), .in_8(4'b0000), .in_9(4'b0000), .in_10(4'b0000),
    .in_11(4'b0000), .in_12(4'b0000), .in_13(4'b0000), .in_14(4'b0000), .in_15(4'b0000),
    .out(multiplexer_1_out));
  Comparator #(.Bits(4)) comparator_1 (.a(State), .b(4'b0000), .eq(comparator_1_eq));  // open: gt, lt
  Comparator #(.Bits(4)) comparator_2 (.a(State), .b(4'b0000));  // open: gt, eq, lt
  Comparator #(.Bits(4)) comparator_3 (.a(State), .b(4'b0001));  // open: gt, eq, lt
  Comparator #(.Bits(4)) comparator_4 (.a(State), .b(4'b0010));  // open: gt, eq, lt
  Comparator #(.Bits(4)) comparator_5 (.a(State), .b(4'b0011));  // open: gt, eq, lt
  Comparator #(.Bits(4)) comparator_6 (.a(State), .b(4'b0100));  // open: gt, eq, lt
  Comparator #(.Bits(4)) comparator_7 (.a(State), .b(4'b0101));  // open: gt, eq, lt
  Comparator #(.Bits(4)) comparator_8 (.a(State), .b(4'b0110));  // open: gt, eq, lt
  D_FF d_ff_2 (.D(1'b0), .C(comparator_1_eq), .Q(CoffeeOut));  // open: nQ
  D_FF d_ff_3 (.D(1'b0), .C(comparator_1_eq), .Q(TeaOut));  // open: nQ
  D_FF #(.Bits(2)) d_ff_4 (.D(2'b00), .C(comparator_1_eq), .Q(Change5));  // open: nQ
  D_FF #(.Bits(2)) d_ff_5 (.D(2'b00), .C(comparator_1_eq), .Q(Change10));  // open: nQ
  D_FF #(.Bits(2)) d_ff_6 (.D(2'b00), .C(comparator_1_eq), .Q(Change20));  // open: nQ
  assign nextStateFrom0001 = reset ? 4'b0000 : 4'bz;  // Driver driver_1
  Comparator #(.Bits(6)) comparator_9 (.a(Balance), .b(6'b101101), .gt(comparator_9_gt));  // open: eq, lt
  Comparator #(.Bits(6)) comparator_10 (.a(Balance), .b(6'b101000), .gt(comparator_10_gt));  // open: eq, lt
  Comparator #(.Bits(6)) comparator_11 (.a(Balance), .b(6'b011110), .gt(comparator_11_gt));  // open: eq, lt
  Comparator #(.Bits(6)) comparator_12 (.a(Balance), .b(6'b011001), .lt(comparator_12_lt));  // open: gt, eq
  Comparator #(.Bits(6)) comparator_13 (.a(Balance), .b(6'b010100), .lt(comparator_13_lt));  // open: gt, eq
  nor nor_1 (nor_1_out, P5_t, P10_t, P20_t, Pcoffee_t_t, Ptea_t_t, reset);
  not not_1 (not_1_out, comparator_9_gt);
  not not_2 (not_2_out, comparator_10_gt);
  not not_3 (not_3_out, comparator_11_gt);
  not not_4 (not_4_out, comparator_12_lt);
  not not_5 (not_5_out, comparator_13_lt);
  and and_1 (and_1_out, P5_t, not_1_out);
  and and_2 (and_2_out, P10_t, not_2_out);
  and and_3 (and_3_out, P20_t, not_3_out);
  and and_4 (and_4_out, PCoffee_t, not_4_out);
  and and_5 (and_5_out, PTea_t, not_5_out);
  Multiplexer multiplexer_2 (.sel(PChange_t), .in_0(1'b1), .in_1(1'b1), .out(multiplexer_2_out[0]));
  D_FF d_ff_7 (.D(P5), .C(clock), .nQ(d_ff_7_nq));  // open: Q
  D_FF d_ff_8 (.D(P10), .C(clock), .nQ(d_ff_8_nq));  // open: Q
  D_FF d_ff_9 (.D(P20), .C(clock), .nQ(d_ff_9_nq));  // open: Q
  D_FF d_ff_10 (.D(Pcoffee), .C(clock), .nQ(d_ff_10_nq));  // open: Q
  assign nextStateFrom0001 = and_1_out ? 4'b0010 : 4'bz;  // Driver driver_2
  assign nextStateFrom0001 = and_2_out ? 4'b0011 : 4'bz;  // Driver driver_3
  assign nextStateFrom0001 = and_3_out ? 4'b0100 : 4'bz;  // Driver driver_4
  assign nextStateFrom0001 = and_4_out ? 4'b0101 : 4'bz;  // Driver driver_5
  assign nextStateFrom0001 = and_5_out ? 4'b0110 : 4'bz;  // Driver driver_6
  assign nextStateFrom0001 = nor_1_out ? multiplexer_2_out : 4'bz;  // Driver driver_7
  and and_6 (and_6_out, P5, d_ff_7_nq);
  and and_7 (and_7_out, P10, d_ff_8_nq);
  and and_8 (and_8_out, P20, d_ff_9_nq);
  and and_9 (and_9_out, Pcoffee, d_ff_10_nq);
  D_FF d_ff_11 (.D(and_6_out), .C(clock), .Q(P5_t));  // open: nQ
  D_FF d_ff_12 (.D(and_7_out), .C(clock), .Q(P10_t));  // open: nQ
  D_FF d_ff_13 (.D(and_8_out), .C(clock), .Q(P20_t));  // open: nQ
  D_FF d_ff_14 (.D(and_9_out), .C(clock), .Q(Pcoffee_t_t));  // open: nQ
  D_FF d_ff_15 (.D(Ptea), .C(clock), .nQ(d_ff_15_nq));  // open: Q
  D_FF d_ff_16 (.D(Pchange), .C(clock), .nQ(d_ff_16_nq));  // open: Q
  D_FF d_ff_17 (.D(Pnext), .C(clock), .nQ(d_ff_17_nq));  // open: Q
  Add #(.Bits(6)) add_1 (.a(Balance), .b(6'b000101), .c_i(1'b0), .s(add_1_s));  // open: c_o
  Add #(.Bits(6)) add_2 (.a(Balance), .b(6'b001010), .c_i(1'b0), .s(add_2_s));  // open: c_o
  Add #(.Bits(6)) add_3 (.a(Balance), .b(6'b010100), .c_i(1'b0), .s(add_3_s));  // open: c_o
  Sub #(.Bits(6)) sub_1 (.a(Balance), .b(6'b011001), .c_i(1'b0), .s(sub_1_s));  // open: c_o
  Sub #(.Bits(6)) sub_2 (.a(Balance), .b(6'b010100), .c_i(1'b0), .s(sub_2_s));  // open: c_o
  and and_10 (and_10_out, Ptea, d_ff_15_nq);
  and and_11 (and_11_out, Pchange, d_ff_16_nq);
  and and_12 (and_12_out, Pnext, d_ff_17_nq);
  D_FF d_ff_18 (.D(and_10_out), .C(clock), .Q(Ptea_t_t));  // open: nQ
  D_FF d_ff_19 (.D(and_11_out), .C(clock), .Q(Pchange_t_t));  // open: nQ
  D_FF d_ff_20 (.D(and_12_out), .C(clock), .Q(Pnext_t));  // open: nQ
  Multiplexer #(.Bits(6), .Selector_Bits(4)) multiplexer_3 (
    .sel(State), .in_0({6{1'b0}}), .in_1(Balance), .in_2(add_1_s), .in_3(add_2_s), .in_4(add_3_s),
    .in_5(sub_1_s), .in_6(sub_2_s), .in_7(Balance), .in_8(Balance), .in_9(Balance), .in_10(Balance),
    .in_11(Balance), .in_12(Balance), .in_13(Balance), .in_14(Balance), .in_15(Balance),
    .out(multiplexer_3_out));
  D_FF #(.Bits(6)) d_ff_21 (.D(multiplexer_3_out), .C(clock_2), .Q(Balance));  // open: nQ
  // Pins of 1 and 4 bits meet at multiplexer_2_out
  // Pins of 1 and 4 bits meet at 4'b0001
  // Pins of 1 and 4 bits meet at 4'b0111
  // also tied to GND on the sheet: {Change5[0], Change5[1], Change10[0], Change10[1], Change20[0], Change20[1], CoffeeOut, TeaOut}
endmodule
