// Digital circuit 09_test.dig as structural Verilog
module _09_test (
  input  clk
);

  wire [1:0] a, d_ff_1_q, multiplexer_1_out;

  Multiplexer #(.Bits(2), .Selector_Bits(2)) multiplexer_1 (
    .sel(d_ff_1_q), .in_0(a), .in_1(a), .in_2(a), .in_3(a), .out(multiplexer_1_out));
  D_FF #(.Bits(2)) d_ff_1 (.D(multiplexer_1_out), .C(clk), .Q(d_ff_1_q));  // open: nQ
  D_FF #(.Bits(2)) d_ff_2 (.D(2'b01), .C(1'b1), .Q(a));  // open: nQ
  D_FF #(.Bits(2)) d_ff_3 (.D(2'b01), .C(1'b1), .Q(a));  // open: nQ
endmodule
