// Digital circuit arithmetic.dig as structural Verilog
module arithmetic (
  input  [3:0] A,
  input  [3:0] B,
  input  [2:0] S,
  input  C,
  output [3:0] O
);

  wire [3:0] add_1_s, add_2_s, add_3_s, add_4_s, add_5_s, add_6_s, multiplexer_1_out, not_1_out, not_2_out;

  Multiplexer #(.Bits(4)) multiplexer_1 (.sel(C), .in_0(4'b1111), .in_1(4'b0000), .out(multiplexer_1_out));
  assign not_1_out = ~B;  // Not not_1, 4 bits wide
  assign not_2_out = ~A;  // Not not_2, 4 bits wide
  Add #(.Bits(4)) add_1 (.a(A), .b(4'b0000), .c_i(C), .s(add_1_s));  // open: c_o
  Add #(.Bits(4)) add_2 (.a(A), .b(multiplexer_1_out), .c_i(1'b0), .s(add_2_s));  // open: c_o
  Add #(.Bits(4)) add_3 (.a(A), .b(B), .c_i(C), .s(add_3_s));  // open: c_o
  Add #(.Bits(4)) add_4 (.a(A), .b(not_1_out), .c_i(C), .s(add_4_s));  // open: c_o
  Add #(.Bits(4)) add_5 (.a(not_2_out), .b(4'b0000), .c_i(C), .s(add_5_s));  // open: c_o
  Add #(.Bits(4)) add_6 (.a(B), .b(4'b0000), .c_i(C), .s(add_6_s));  // open: c_o
  Multiplexer #(.Selector_Bits(3), .Bits(4)) multiplexer_2 (
    .sel(S), .in_0(add_1_s), .in_1(add_2_s), .in_2(add_3_s), .in_3(add_4_s), .in_4(add_5_s), .in_5(add_6_s),
    .in_6({A[2:0], 1'b0}), .in_7({1'b0, A[3:1]}), .out(O));
endmodule
