// Digital circuit 02.dig as structural Verilog
module _02 (
  input  A,
  input  B,
  input  Clr,
  input  Clock,
  output Z
);

  wire add_1_c_o, add_1_s, d_ff_1_q, multiplexer_1_out, not_1_out;

  Add add_1 (.a(A), .b(B), .c_i(d_ff_1_q), .s(add_1_s), .c_o(add_1_c_o));
  Multiplexer multiplexer_1 (.sel(not_1_out), .in_0(add_1_c_o), .in_1(1'b0), .out(multiplexer_1_out));
  D_FF d_ff_1 (.D(multiplexer_1_out), .C(Clock), .Q(d_ff_1_q));  // open: nQ
  Multiplexer multiplexer_2 (.sel(Clr), .in_0(1'b0), .in_1(add_1_s), .out(Z));
  not not_1 (not_1_out, Clr);
endmodule
