// Digital circuit 04.dig as structural Verilog
module _04 (
  input  P,
  input  Clr,
  input  clock,
  output Z
);

  wire and_1_out, d_ff_1_q, d_ff_2_q, multiplexer_1_out, xor_1_out;

  D_FF d_ff_1 (.D(P), .C(clock), .Q(d_ff_1_q));  // open: nQ
  and and_1 (and_1_out, d_ff_1_q, ~Clr);  // And
  D_FF d_ff_2 (.D(and_1_out), .C(clock), .Q(d_ff_2_q));  // open: nQ
  xor xor_1 (xor_1_out, and_1_out, d_ff_2_q);
  Multiplexer multiplexer_1 (.sel(and_1_out), .in_0(1'b0), .in_1(xor_1_out), .out(multiplexer_1_out));
  D_FF d_ff_3 (.D(multiplexer_1_out), .C(clock), .Q(Z));  // open: nQ
endmodule
