// Digital circuit 09.dig as structural Verilog
module _09 (
  input  P5,
  input  reset,
  input  clock,
  input  P10,
  input  P20,
  input  Pcoffee,
  input  Ptea,
  input  Pchange,
  input  Pnext,
  output [5:0] Balance,
  output CoffeeOut,
  output TeaOut,
  output [1:0] Change5,
  output [1:0] Change10,
  output [1:0] Change20,
  output [3:0] State
);

  wire and_1_out, and_2_out, and_3_out, and_4_out, and_5_out, and_6_out, and_7_out, and_8_out, and_9_out,
       and_10_out, and_11_out, and_12_out, and_13_out, comparator_1_gt, comparator_2_gt, comparator_3_gt,
       comparator_4_lt, comparator_5_lt, comparator_19_lt, comparator_20_lt, comparator_21_lt, d_ff_2_nq,
       d_ff_3_nq, d_ff_4_nq, d_ff_5_nq, d_ff_10_nq, d_ff_11_nq, d_ff_12_nq, multiplexer_6_out,
       multiplexer_7_out, nor_1_out, nor_2_out, nor_3_out, not_1_out, not_2_out, not_3_out, not_4_out,
       not_5_out, not_6_out, not_7_out, not_8_out, P5_t, P10_t, P20_t, Pchange_t, Pcoffee_t, Pnext_t, Ptea_t;
  wire [1:0] add_4_s, add_5_s, add_6_s, multiplexer_8_out, multiplexer_9_out, multiplexer_10_out;
  wire [3:0] multiplexer_1_out, multiplexer_2_out, multiplexer_3_out, multiplexer_4_out, nextStateFrom0001,
       nextStateFrom0111, nextStateFrom1101;
  wire [5:0] add_1_s, add_2_s, add_3_s, multiplexer_5_out, sub_1_s, sub_2_s, sub_3_s, sub_4_s, sub_5_s;

  Comparator #(.Bits(6)) comparator_1 (.a(Balance), .b(6'b101101), .gt(comparator_1_gt));  // open: eq, lt
  Comparator #(.Bits(6)) comparator_2 (.a(Balance), .b(6'b101000), .gt(comparator_2_gt));  // open: eq, lt
  Comparator #(.Bits(6)) comparator_3 (.a(Balance), .b(6'b011110), .gt(comparator_3_gt));  // open: eq, lt
  Comparator #(.Bits(6)) comparator_4 (.a(Balance), .b(6'b011001), .lt(comparator_4_lt));  // open: gt, eq
  Comparator #(.Bits(6)) comparator_5 (.a(Balance), .b(6'b010100), .lt(comparator_5_lt));  // open: gt, eq
  assign nextStateFrom0001 = reset ? 4'b0000 : 4'bz;  // Driver driver_1
  not not_1 (not_1_out, comparator_1_gt);
  not not_2 (not_2_out, comparator_2_gt);
  not not_3 (not_3_out, comparator_3_gt);
  not not_4 (not_4_out, comparator_4_lt);
  not not_5 (not_5_out, comparator_5_lt);
  and and_1 (and_1_out, P5_t, not_1_out);
  and and_2 (and_2_out, P10_t, not_2_out);
  and and_3 (and_3_out, P20_t, not_3_out);
  and and_4 (and_4_out, Pcoffee_t, not_4_out);
  and and_5 (and_5_out, Ptea_t, not_5_out);
  Comparator #(.Bits(4)) comparator_6 (.a(State), .b(4'b0000));  // open: gt, eq, lt
  Comparator #(.Bits(4)) comparator_7 (.a(State), .b(4'b0001));  // open: gt, eq, lt
  assign nextStateFrom0001 = and_1_out ? 4'b0010 : 4'bz;  // Driver driver_2
  assign nextStateFrom0001 = and_2_out ? 4'b0011 : 4'bz;  // Driver driver_3
  assign nextStateFrom0001 = and_3_out ? 4'b0100 : 4'bz;  // Driver driver_4
  assign nextStateFrom0001 = and_4_out ? 4'b0101 : 4'bz;  // Driver driver_5
  assign nextStateFrom0001 = and_5_out ? 4'b0110 : 4'bz;  // Driver driver_6
  nor nor_1 (nor_1_out, reset, and_1_out, and_2_out, and_3_out, and_4_out, and_5_out);
  Multiplexer #(.Bits(4)) multiplexer_1 (.sel(Pchange_t), .in_0(4'b0001), .in_1(4'b1111), .out(multiplexer_1_out));
  assign nextStateFrom0001 = nor_1_out ? multiplexer_1_out : 4'bz;  // Driver driver_7
  Comparator #(.Bits(4)) comparator_8 (.a(State), .b(4'b0010));  // open: gt, eq, lt
  Comparator #(.Bits(4)) comparator_9 (.a(State), .b(4'b0011));  // open: gt, eq, lt
  Comparator #(.Bits(4)) comparator_10 (.a(State), .b(4'b0100));  // open: gt, eq, lt
  Comparator #(.Bits(4)) comparator_11 (.a(State), .b(4'b0101));  // open: gt, eq, lt
  Comparator #(.Bits(4)) comparator_12 (.a(State), .b(4'b0110));  // open: gt, eq, lt
  Comparator #(.Bits(4)) comparator_13 (.a(State), .b(4'b0111));  // open: gt, eq, lt
  Comparator #(.Bits(4)) comparator_14 (.a(State), .b(4'b1101));  // open: gt, eq, lt
  Comparator #(.Bits(4)) comparator_15 (.a(State), .b(4'b1000));  // open: gt, eq, lt
  Comparator #(.Bits(4)) comparator_16 (.a(State), .b(4'b1001));  // open: gt, eq, lt
  Comparator #(.Bits(4)) comparator_17 (.a(State), .b(4'b1100));  // open: gt, eq, lt
  Comparator #(.Bits(4)) comparator_18 (.a(State), .b(4'b1111));  // open: gt, eq, lt
  Multiplexer #(.Selector_Bits(4), .Bits(4)) multiplexer_2 (
    .sel(State), .in_0(4'b0001), .in_1(nextStateFrom0001), .in_2(4'b0001), .in_3(4'b0001), .in_4(4'b0001),
    .in_5(4'b0111), .in_6(4'b0111), .in_7(nextStateFrom0111), .in_8(4'b1101), .in_9(4'b1101),
    .in_10(4'b0001), .in_11(4'b0001), .in_12(4'b1101), .in_13(nextStateFrom1101), .in_14(4'b0001),
    .in_15(4'b1101), .out(multiplexer_2_out));
  D_FF #(.Bits(4)) d_ff_1 (.D(multiplexer_2_out), .C(clock), .Q(State));  // open: nQ
  assign nextStateFrom0111 = reset ? 4'b0000 : 4'bz;  // Driver driver_8
  assign nextStateFrom0111 = Pnext_t ? 4'b0001 : 4'bz;  // Driver driver_9
  Comparator #(.Bits(6)) comparator_19 (.a(Balance), .b(6'b010100), .lt(comparator_19_lt));  // open: gt, eq
  Comparator #(.Bits(6)) comparator_20 (.a(Balance), .b(6'b001010), .lt(comparator_20_lt));  // open: gt, eq
  Comparator #(.Bits(6)) comparator_21 (.a(Balance), .b(6'b000101), .lt(comparator_21_lt));  // open: gt, eq
  nor nor_2 (nor_2_out, reset, Pnext_t);
  not not_6 (not_6_out, comparator_20_lt);
  not not_7 (not_7_out, comparator_21_lt);
  Multiplexer #(.Bits(4)) multiplexer_3 (.sel(Pchange_t), .in_0(4'b0111), .in_1(4'b1111), .out(multiplexer_3_out));
  not not_8 (not_8_out, comparator_19_lt);
  and and_6 (and_6_out, comparator_19_lt, not_6_out);
  D_FF d_ff_2 (.D(P5), .C(clock), .nQ(d_ff_2_nq));  // open: Q
  D_FF d_ff_3 (.D(P10), .C(clock), .nQ(d_ff_3_nq));  // open: Q
  D_FF d_ff_4 (.D(P20), .C(clock), .nQ(d_ff_4_nq));  // open: Q
  D_FF d_ff_5 (.D(Pcoffee), .C(clock), .nQ(d_ff_5_nq));  // open: Q
  assign nextStateFrom0111 = nor_2_out ? multiplexer_3_out : 4'bz;  // Driver driver_10
  assign nextStateFrom1101 = not_8_out ? 4'b1100 : 4'bz;  // Driver driver_11
  assign nextStateFrom1101 = and_6_out ? 4'b1000 : 4'bz;  // Driver driver_12
  and and_7 (and_7_out, P5, d_ff_2_nq);
  and and_8 (and_8_out, P10, d_ff_3_nq);
  and and_9 (and_9_out, P20, d_ff_4_nq);
  and and_10 (and_10_out, Pcoffee, d_ff_5_nq);
  nor nor_3 (nor_3_out, not_8_out, and_6_out);
  Multiplexer #(.Bits(4)) multiplexer_4 (.sel(not_7_out), .in_0(4'b0001), .in_1(4'b1001), .out(multiplexer_4_out));
  D_FF d_ff_6 (.D(and_7_out), .C(clock), .Q(P5_t));  // open: nQ
  D_FF d_ff_7 (.D(and_8_out), .C(clock), .Q(P10_t));  // open: nQ
  D_FF d_ff_8 (.D(and_9_out), .C(clock), .Q(P20_t));  // open: nQ
  D_FF d_ff_9 (.D(and_10_out), .C(clock), .Q(Pcoffee_t));  // open: nQ
  assign nextStateFrom1101 = nor_3_out ? multiplexer_4_out : 4'bz;  // Driver driver_13
  Add #(.Bits(6)) add_1 (.a(Balance), .b(6'b000101), .c_i(1'b0), .s(add_1_s));  // open: c_o
  Add #(.Bits(6)) add_2 (.a(Balance), .b(6'b001010), .c_i(1'b0), .s(add_2_s));  // open: c_o
  Add #(.Bits(6)) add_3 (.a(Balance), .b(6'b010100), .c_i(1'b0), .s(add_3_s));  // open: c_o
  Sub #(.Bits(6)) sub_1 (.a(Balance), .b(6'b011001), .c_i(1'b0), .s(sub_1_s));  // open: c_o
  Sub #(.Bits(6)) sub_2 (.a(Balance), .b(6'b010100), .c_i(1'b0), .s(sub_2_s));  // open: c_o
  Sub #(.Bits(6)) sub_3 (.a(Balance), .b(6'b001010), .c_i(1'b0), .s(sub_3_s));  // open: c_o
  Sub #(.Bits(6)) sub_4 (.a(Balance), .b(6'b000101), .c_i(1'b0), .s(sub_4_s));  // open: c_o
  Sub #(.Bits(6)) sub_5 (.a(Balance), .b(6'b010100), .c_i(1'b0), .s(sub_5_s));  // open: c_o
  D_FF d_ff_10 (.D(Ptea), .C(clock), .nQ(d_ff_10_nq));  // open: Q
  D_FF d_ff_11 (.D(Pchange), .C(clock), .nQ(d_ff_11_nq));  // open: Q
  D_FF d_ff_12 (.D(Pnext), .C(clock), .nQ(d_ff_12_nq));  // open: Q
  and and_11 (and_11_out, Ptea, d_ff_10_nq);
  and and_12 (and_12_out, Pchange, d_ff_11_nq);
  and and_13 (and_13_out, Pnext, d_ff_12_nq);
  Multiplexer #(.Selector_Bits(4), .Bits(6)) multiplexer_5 (
    .sel(State), .in_0({6{1'b0}}), .in_1(Balance), .in_2(add_1_s), .in_3(add_2_s), .in_4(add_3_s),
    .in_5(sub_1_s), .in_6(sub_2_s), .in_7(Balance), .in_8(sub_3_s), .in_9(sub_4_s), .in_10(Balance),
    .in_11(Balance), .in_12(sub_5_s), .in_13(Balance), .in_14(Balance), .in_15(Balance),
    .out(multiplexer_5_out));
  Multiplexer #(.Selector_Bits(4)) multiplexer_6 (
    .sel(State), .in_0(1'b0), .in_1(1'b0), .in_2(CoffeeOut), .in_3(CoffeeOut), .in_4(CoffeeOut), .in_5(1'b1),
    .in_6(CoffeeOut), .in_7(CoffeeOut), .in_8(CoffeeOut), .in_9(CoffeeOut), .in_10(CoffeeOut),
    .in_11(CoffeeOut), .in_12(CoffeeOut), .in_13(CoffeeOut), .in_14(CoffeeOut), .in_15(CoffeeOut),
    .out(multiplexer_6_out));
  Multiplexer #(.Selector_Bits(4)) multiplexer_7 (
    .sel(State), .in_0(1'b0), .in_1(1'b0), .in_2(TeaOut), .in_3(TeaOut), .in_4(TeaOut), .in_5(TeaOut),
    .in_6(1'b1), .in_7(TeaOut), .in_8(TeaOut), .in_9(TeaOut), .in_10(TeaOut), .in_11(TeaOut), .in_12(TeaOut),
    .in_13(TeaOut), .in_14(TeaOut), .in_15(TeaOut), .out(multiplexer_7_out));
  D_FF d_ff_13 (.D(and_11_out), .C(clock), .Q(Ptea_t));  // open: nQ
  D_FF d_ff_14 (.D(and_12_out), .C(clock), .Q(Pchange_t));  // open: nQ
  D_FF d_ff_15 (.D(and_13_out), .C(clock), .Q(Pnext_t));  // open: nQ
  D_FF #(.Bits(6)) d_ff_16 (.D(multiplexer_5_out), .C(clock), .Q(Balance));  // open: nQ
  D_FF d_ff_17 (.D(multiplexer_6_out), .C(clock), .Q(CoffeeOut));  // open: nQ
  D_FF d_ff_18 (.D(multiplexer_7_out), .C(clock), .Q(TeaOut));  // open: nQ
  Add #(.Bits(2)) add_4 (.a(Change20), .b(2'b01), .c_i(1'b0), .s(add_4_s));  // open: c_o
  Add #(.Bits(2)) add_5 (.a(Change10), .b(2'b01), .c_i(1'b0), .s(add_5_s));  // open: c_o
  Add #(.Bits(2)) add_6 (.a(Change5), .b(2'b01), .c_i(1'b0), .s(add_6_s));  // open: c_o
  Multiplexer #(.Selector_Bits(4), .Bits(2)) multiplexer_8 (
    .sel(State), .in_0(2'b00), .in_1(Change20), .in_2(Change20), .in_3(Change20), .in_4(Change20),
    .in_5(Change20), .in_6(Change20), .in_7(Change20), .in_8(Change20), .in_9(Change20), .in_10(Change20),
    .in_11(Change20), .in_12(add_4_s), .in_13(Change20), .in_14(Change20), .in_15(2'b00),
    .out(multiplexer_8_out));
  Multiplexer #(.Selector_Bits(4), .Bits(2)) multiplexer_9 (
    .sel(State), .in_0(2'b00), .in_1(Change10), .in_2(Change10), .in_3(Change10), .in_4(Change10),
    .in_5(Change10), .in_6(Change10), .in_7(Change10), .in_8(add_5_s), .in_9(Change10), .in_10(Change10),
    .in_11(Change10), .in_12(Change10), .in_13(Change10), .in_14(Change10), .in_15(2'b00),
    .out(multiplexer_9_out));
  Multiplexer #(.Selector_Bits(4), .Bits(2)) multiplexer_10 (
    .sel(State), .in_0(2'b00), .in_1(Change5), .in_2(Change5), .in_3(Change5), .in_4(Change5),
    .in_5(Change5), .in_6(Change5), .in_7(Change5), .in_8(Change5), .in_9(add_6_s), .in_10(Change5),
    .in_11(Change5), .in_12(Change5), .in_13(Change5), .in_14(Change5), .in_15(2'b00),
    .out(multiplexer_10_out));
  D_FF #(.Bits(2)) d_ff_19 (.D(multiplexer_8_out), .C(clock), .Q(Change20));  // open: nQ
  D_FF #(.Bits(2)) d_ff_20 (.D(multiplexer_9_out), .C(clock), .Q(Change10));  // open: nQ
  D_FF #(.Bits(2)) d_ff_21 (.D(multiplexer_10_out), .C(clock), .Q(Change5));  // open: nQ
endmodule

/* Test case test 1:
clock reset P5 P10 P20 Pcoffee Ptea Pchange Pnext Balance CoffeeOut TeaOut Change5 Change10 Change20
0 1 0 0 0 0 0 0 0 x x x x x x
1 1 0 0 0 0 0 0 0 0 0 0 0 0 0
0 0 1 0 0 0 0 0 0 0 0 0 0 0 0
1 0 1 0 0 0 0 0 0 0 0 0 0 0 0
0 0 0 0 0 0 0 0 0 x x x x x x
1 0 0 0 0 0 0 0 0 x x x x x x
0 0 0 0 0 0 0 0 0 x x x x x x
1 0 0 0 0 0 0 0 0 x x x x x x
0 0 0 0 0 0 0 0 0 x x x x x x
1 0 0 0 0 0 0 0 0 x x x x x x
0 0 0 0 0 0 0 0 0 x x x x x x
1 0 0 0 0 0 0 0 0 x x x x x x
0 0 0 0 0 0 0 0 0 x x x x x x
1 0 0 0 0 0 0 0 0 x x x x x x
0 0 0 0 0 0 0 0 0 x x x x x x
1 0 0 0 0 0 0 0 0 x x x x x x
0 0 0 0 0 0 0 0 0 x x x x x x
1 0 0 0 0 0 0 0 0 x x x x x x
0 0 0 0 0 0 0 0 0 x x x x x x
1 0 0 0 0 0 0 0 0 x x x x x x
0 0 0 0 0 0 0 0 0 x x x x x x
1 0 0 0 0 0 0 0 0 x x x x x x
0 0 0 0 0 0 0 0 0 x x x x x x
1 0 0 0 0 0 0 0 0 x x x x x x
0 0 0 0 0 0 0 0 0 x x x x x x
1 0 0 0 0 0 0 0 0 x x x x x x
0 0 0 0 0 0 0 0 0 x x x x x x
1 0 0 0 0 0 0 0 0 x x x x x x
0 0 0 0 0 0 0 0 0 x x x x x x
1 0 0 0 0 0 0 0 0 x x x x x x
0 0 0 0 0 0 0 0 0 x x x x x x
1 0 0 0 0 0 0 0 0 x x x x x x
0 0 0 0 0 0 0 0 0 x x x x x x
1 0 0 0 0 0 0 0 0 x x x x x x
0 0 0 0 0 0 0 0 0 x x x x x x
1 0 0 0 0 0 0 0 0 x x x x x x
0 0 0 0 0 0 0 0 0 x x x x x x
1 0 0 0 0 0 0 0 0 x x x x x x
0 0 0 0 0 0 0 0 0 x x x x x x
1 0 0 0 0 0 0 0 0 x x x x x x
0 0 0 0 0 0 0 0 0 x x x x x x
1 0 0 0 0 0 0 0 0 x x x x x x
0 0 0 0 0 0 0 0 0 x x x x x x
1 0 0 0 0 0 0 0 0 x x x x x x
0 0 0 0 0 0 0 0 0 5 0 0 0 0 0
1 0 0 0 0 0 0 0 0 5 0 0 0 0 0
0 0 0 1 0 0 0 0 0 5 0 0 0 0 0
1 0 0 1 0 0 0 0 0 5 0 0 0 0 0
0 0 0 0 0 0 0 0 0 x x x x x x
1 0 0 0 0 0 0 0 0 x x x x x x
0 0 0 0 0 0 0 0 0 x x x x x x
1 0 0 0 0 0 0 0 0 x x x x x x
0 0 0 0 0 0 0 0 0 x x x x x x
1 0 0 0 0 0 0 0 0 x x x x x x
0 0 0 0 0 0 0 0 0 x x x x x x
1 0 0 0 0 0 0 0 0 x x x x x x
0 0 0 0 0 0 0 0 0 x x x x x x
1 0 0 0 0 0 0 0 0 x x x x x x
0 0 0 0 0 0 0 0 0 x x x x x x
1 0 0 0 0 0 0 0 0 x x x x x x
0 0 0 0 0 0 0 0 0 x x x x x x
1 0 0 0 0 0 0 0 0 x x x x x x
0 0 0 0 0 0 0 0 0 x x x x x x
1 0 0 0 0 0 0 0 0 x x x x x x
0 0 0 0 0 0 0 0 0 x x x x x x
1 0 0 0 0 0 0 0 0 x x x x x x
0 0 0 0 0 0 0 0 0 x x x x x x
1 0 0 0 0 0 0 0 0 x x x x x x
0 0 0 0 0 0 0 0 0 x x x x x x
1 0 0 0 0 0 0 0 0 x x x x x x
0 0 0 0 0 0 0 0 0 x x x x x x
1 0 0 0 0 0 0 0 0 x x x x x x
0 0 0 0 0 0 0 0 0 x x x x x x
1 0 0 0 0 0 0 0 0 x x x x x x
0 0 0 0 0 0 0 0 0 x x x x x x
1 0 0 0 0 0 0 0 0 x x x x x x
0 0 0 0 0 0 0 0 0 x x x x x x
1 0 0 0 0 0 0 0 0 x x x x x x
0 0 0 0 0 0 0 0 0 x x x x x x
1 0 0 0 0 0 0 0 0 x x x x x x
0 0 0 0 0 0 0 0 0 x x x x x x
1 0 0 0 0 0 0 0 0 x x x x x x
0 0 0 0 0 0 0 0 0 x x x x x x
1 0 0 0 0 0 0 0 0 x x x x x x
0 0 0 0 0 0 0 0 0 x x x x x x
1 0 0 0 0 0 0 0 0 x x x x x x
0 0 0 0 0 0 0 0 0 x x x x x x
1 0 0 0 0 0 0 0 0 x x x x x x
0 0 0 0 0 0 0 0 0 15 0 0 0 0 0
1 0 0 0 0 0 0 0 0 15 0 0 0 0 0
0 0 0 0 1 0 0 0 0 15 0 0 0 0 0
1 0 0 0 1 0 0 0 0 15 0 0 0 0 0
0 0 0 0 0 0 0 0 0 x x x x x x
1 0 0 0 0 0 0 0 0 x x x x x x
0 0 0 0 0 0 0 0 0 x x x x x x
1 0 0 0 0 0 0 0 0 x x x x x x
0 0 0 0 0 0 0 0 0 x x x x x x
1 0 0 0 0 0 0 0 0 x x x x x x
0 0 0 0 0 0 0 0 0 x x x x x x
1 0 0 0 0 0 0 0 0 x x x x x x
0 0 0 0 0 0 0 0 0 x x x x x x
1 0 0 0 0 0 0 0 0 x x x x x x
0 0 0 0 0 0 0 0 0 x x x x x x
1 0 0 0 0 0 0 0 0 x x x x x x
0 0 0 0 0 0 0 0 0 x x x x x x
1 0 0 0 0 0 0 0 0 x x x x x x
0 0 0 0 0 0 0 0 0 x x x x x x
1 0 0 0 0 0 0 0 0 x x x x x x
0 0 0 0 0 0 0 0 0 x x x x x x
1 0 0 0 0 0 0 0 0 x x x x x x
0 0 0 0 0 0 0 0 0 x x x x x x
1 0 0 0 0 0 0 0 0 x x x x x x
0 0 0 0 0 0 0 0 0 x x x x x x
1 0 0 0 0 0 0 0 0 x x x x x x
0 0 0 0 0 0 0 0 0 x x x x x x
1 0 0 0 0 0 0 0 0 x x x x x x
0 0 0 0 0 0 0 0 0 x x x x x x
1 0 0 0 0 0 0 0 0 x x x x x x
0 0 0 0 0 0 0 0 0 x x x x x x
1 0 0 0 0 0 0 0 0 x x x x x x
0 0 0 0 0 0 0 0 0 x x x x x x
1 0 0 0 0 0 0 0 0 x x x x x x
0 0 0 0 0 0 0 0 0 x x x x x x
1 0 0 0 0 0 0 0 0 x x x x x x
0 0 0 0 0 0 0 0 0 x x x x x x
1 0 0 0 0 0 0 0 0 x x x x x x
0 0 0 0 0 0 0 0 0 x x x x x x
1 0 0 0 0 0 0 0 0 x x x x x x
0 0 0 0 0 0 0 0 0 x x x x x x
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*/

/* Test case test 2:
clock reset P5 P10 P20 Pcoffee Ptea Pchange Pnext Balance CoffeeOut TeaOut Change5 Change10 Change20
0 1 0 0 0 0 0 0 0 x x x x x x
1 1 0 0 0 0 0 0 0 0 0 0 0 0 0
0 0 0 0 0 1 0 0 0 0 0 0 0 0 0
1 0 0 0 0 1 0 0 0 0 0 0 0 0 0
0 0 0 0 0 0 0 0 0 x x x x x x
1 0 0 0 0 0 0 0 0 x x x x x x
0 0 0 0 0 0 0 0 0 x x x x x x
1 0 0 0 0 0 0 0 0 x x x x x x
0 0 0 0 0 0 0 0 0 x x x x x x
1 0 0 0 0 0 0 0 0 x x x x x x
0 0 0 0 0 0 0 0 0 x x x x x x
1 0 0 0 0 0 0 0 0 x x x x x x
0 0 0 0 0 0 0 0 0 x x x x x x
1 0 0 0 0 0 0 0 0 x x x x x x
0 0 0 0 0 0 0 0 0 x x x x x x
1 0 0 0 0 0 0 0 0 x x x x x x
0 0 0 0 0 0 0 0 0 x x x x x x
1 0 0 0 0 0 0 0 0 x x x x x x
0 0 0 0 0 0 0 0 0 x x x x x x
1 0 0 0 0 0 0 0 0 x x x x x x
0 0 0 0 0 0 0 0 0 x x x x x x
1 0 0 0 0 0 0 0 0 x x x x x x
0 0 0 0 0 0 0 0 0 x x x x x x
1 0 0 0 0 0 0 0 0 x x x x x x
0 0 0 0 0 0 0 0 0 x x x x x x
1 0 0 0 0 0 0 0 0 x x x x x x
0 0 0 0 0 0 0 0 0 x x x x x x
1 0 0 0 0 0 0 0 0 x x x x x x
0 0 0 0 0 0 0 0 0 x x x x x x
1 0 0 0 0 0 0 0 0 x x x x x x
0 0 0 0 0 0 0 0 0 x x x x x x
1 0 0 0 0 0 0 0 0 x x x x x x
0 0 0 0 0 0 0 0 0 x x x x x x
1 0 0 0 0 0 0 0 0 x x x x x x
0 0 0 0 0 0 0 0 0 x x x x x x
1 0 0 0 0 0 0 0 0 x x x x x x
0 0 0 0 0 0 0 0 0 x x x x x x
1 0 0 0 0 0 0 0 0 x x x x x x
0 0 0 0 0 0 0 0 0 x x x x x x
1 0 0 0 0 0 0 0 0 x x x x x x
0 0 0 0 0 0 0 0 0 x x x x x x
1 0 0 0 0 0 0 0 0 x x x x x x
0 0 0 0 0 0 0 0 0 x x x x x x
1 0 0 0 0 0 0 0 0 x x x x x x
0 0 0 0 0 0 0 0 0 0 0 0 0 0 0
1 0 0 0 0 0 0 0 0 0 0 0 0 0 0
0 0 0 0 0 0 1 0 0 0 0 0 0 0 0
1 0 0 0 0 0 1 0 0 0 0 0 0 0 0
0 0 0 0 0 0 0 0 0 x x x x x x
1 0 0 0 0 0 0 0 0 x x x x x x
0 0 0 0 0 0 0 0 0 x x x x x x
1 0 0 0 0 0 0 0 0 x x x x x x
0 0 0 0 0 0 0 0 0 x x x x x x
1 0 0 0 0 0 0 0 0 x x x x x x
0 0 0 0 0 0 0 0 0 x x x x x x
1 0 0 0 0 0 0 0 0 x x x x x x
0 0 0 0 0 0 0 0 0 x x x x x x
1 0 0 0 0 0 0 0 0 x x x x x x
0 0 0 0 0 0 0 0 0 x x x x x x
1 0 0 0 0 0 0 0 0 x x x x x x
0 0 0 0 0 0 0 0 0 x x x x x x
1 0 0 0 0 0 0 0 0 x x x x x x
0 0 0 0 0 0 0 0 0 x x x x x x
1 0 0 0 0 0 0 0 0 x x x x x x
0 0 0 0 0 0 0 0 0 x x x x x x
1 0 0 0 0 0 0 0 0 x x x x x x
0 0 0 0 0 0 0 0 0 x x x x x x
1 0 0 0 0 0 0 0 0 x x x x x x
0 0 0 0 0 0 0 0 0 x x x x x x
1 0 0 0 0 0 0 0 0 x x x x x x
0 0 0 0 0 0 0 0 0 x x x x x x
1 0 0 0 0 0 0 0 0 x x x x x x
0 0 0 0 0 0 0 0 0 x x x x x x
1 0 0 0 0 0 0 0 0 x x x x x x
0 0 0 0 0 0 0 0 0 x x x x x x
1 0 0 0 0 0 0 0 0 x x x x x x
0 0 0 0 0 0 0 0 0 x x x x x x
1 0 0 0 0 0 0 0 0 x x x x x x
0 0 0 0 0 0 0 0 0 x x x x x x
1 0 0 0 0 0 0 0 0 x x x x x x
0 0 0 0 0 0 0 0 0 x x x x x x
1 0 0 0 0 0 0 0 0 x x x x x x
0 0 0 0 0 0 0 0 0 x x x x x x
1 0 0 0 0 0 0 0 0 x x x x x x
0 0 0 0 0 0 0 0 0 x x x x x x
1 0 0 0 0 0 0 0 0 x x x x x x
0 0 0 0 0 0 0 0 0 x x x x x x
1 0 0 0 0 0 0 0 0 x x x x x x
0 0 0 0 0 0 0 0 0 0 0 0 0 0 0
1 0 0 0 0 0 0 0 0 0 0 0 0 0 0
0 0 0 0 1 0 0 0 0 0 0 0 0 0 0
1 0 0 0 1 0 0 0 0 0 0 0 0 0 0
0 0 0 0 0 0 0 0 0 x x x x x x
1 0 0 0 0 0 0 0 0 x x x x x x
0 0 0 0 0 0 0 0 0 x x x x x x
1 0 0 0 0 0 0 0 0 x x x x x x
0 0 0 0 0 0 0 0 0 x x x x x x
1 0 0 0 0 0 0 0 0 x x x x x x
0 0 0 0 0 0 0 0 0 x x x x x x
1 0 0 0 0 0 0 0 0 x x x x x x
0 0 0 0 0 0 0 0 0 x x x x x x
1 0 0 0 0 0 0 0 0 x x x x x x
0 0 0 0 0 0 0 0 0 x x x x x x
1 0 0 0 0 0 0 0 0 x x x x x x
0 0 0 0 0 0 0 0 0 x x x x x x
1 0 0 0 0 0 0 0 0 x x x x x x
0 0 0 0 0 0 0 0 0 x x x x x x
1 0 0 0 0 0 0 0 0 x x x x x x
0 0 0 0 0 0 0 0 0 x x x x x x
1 0 0 0 0 0 0 0 0 x x x x x x
0 0 0 0 0 0 0 0 0 x x x x x x
1 0 0 0 0 0 0 0 0 x x x x x x
0 0 0 0 0 0 0 0 0 x x x x x x
1 0 0 0 0 0 0 0 0 x x x x x x
0 0 0 0 0 0 0 0 0 x x x x x x
1 0 0 0 0 0 0 0 0 x x x x x x
0 0 0 0 0 0 0 0 0 x x x x x x
1 0 0 0 0 0 0 0 0 x x x x x x
0 0 0 0 0 0 0 0 0 x x x x x x
1 0 0 0 0 0 0 0 0 x x x x x x
0 0 0 0 0 0 0 0 0 x x x x x x
1 0 0 0 0 0 0 0 0 x x x x x x
0 0 0 0 0 0 0 0 0 x x x x x x
1 0 0 0 0 0 0 0 0 x x x x x x
0 0 0 0 0 0 0 0 0 x x x x x x
1 0 0 0 0 0 0 0 0 x x x x x x
0 0 0 0 0 0 0 0 0 x x x x x x
1 0 0 0 0 0 0 0 0 x x x x x x
0 0 0 0 0 0 0 0 0 x x x x x x
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*/

/* Test case test 3:
clock reset P5 P10 P20 Pcoffee Ptea Pchange Pnext Balance CoffeeOut TeaOut Change5 Change10 Change20
0 1 0 0 0 0 0 0 0 x x x x x x
1 1 0 0 0 0 0 0 0 0 0 0 0 0 0
0 0 1 0 0 0 0 0 0 0 0 0 0 0 0
1 0 1 0 0 0 0 0 0 0 0 0 0 0 0
0 0 0 0 0 0 0 0 0 x x x x x x
1 0 0 0 0 0 0 0 0 x x x x x x
0 0 0 0 0 0 0 0 0 x x x x x x
1 0 0 0 0 0 0 0 0 x x x x x x
0 0 0 0 0 0 0 0 0 x x x x x x
1 0 0 0 0 0 0 0 0 x x x x x x
0 0 0 0 0 0 0 0 0 x x x x x x
1 0 0 0 0 0 0 0 0 x x x x x x
0 0 0 0 0 0 0 0 0 x x x x x x
1 0 0 0 0 0 0 0 0 x x x x x x
0 0 0 0 0 0 0 0 0 x x x x x x
1 0 0 0 0 0 0 0 0 x x x x x x
0 0 0 0 0 0 0 0 0 x x x x x x
1 0 0 0 0 0 0 0 0 x x x x x x
0 0 0 0 0 0 0 0 0 x x x x x x
1 0 0 0 0 0 0 0 0 x x x x x x
0 0 0 0 0 0 0 0 0 x x x x x x
1 0 0 0 0 0 0 0 0 x x x x x x
0 0 0 0 0 0 0 0 0 x x x x x x
1 0 0 0 0 0 0 0 0 x x x x x x
0 0 0 0 0 0 0 0 0 x x x x x x
1 0 0 0 0 0 0 0 0 x x x x x x
0 0 0 0 0 0 0 0 0 x x x x x x
1 0 0 0 0 0 0 0 0 x x x x x x
0 0 0 0 0 0 0 0 0 x x x x x x
1 0 0 0 0 0 0 0 0 x x x x x x
0 0 0 0 0 0 0 0 0 x x x x x x
1 0 0 0 0 0 0 0 0 x x x x x x
0 0 0 0 0 0 0 0 0 x x x x x x
1 0 0 0 0 0 0 0 0 x x x x x x
0 0 0 0 0 0 0 0 0 x x x x x x
1 0 0 0 0 0 0 0 0 x x x x x x
0 0 0 0 0 0 0 0 0 x x x x x x
1 0 0 0 0 0 0 0 0 x x x x x x
0 0 0 0 0 0 0 0 0 x x x x x x
1 0 0 0 0 0 0 0 0 x x x x x x
0 0 0 0 0 0 0 0 0 x x x x x x
1 0 0 0 0 0 0 0 0 x x x x x x
0 0 0 0 0 0 0 0 0 x x x x x x
1 0 0 0 0 0 0 0 0 x x x x x x
0 0 0 0 0 0 0 0 0 5 0 0 0 0 0
1 0 0 0 0 0 0 0 0 5 0 0 0 0 0
0 0 0 0 0 0 0 1 0 5 0 0 0 0 0
1 0 0 0 0 0 0 1 0 5 0 0 0 0 0
0 0 0 0 0 0 0 0 0 x x x x x x
1 0 0 0 0 0 0 0 0 x x x x x x
0 0 0 0 0 0 0 0 0 x x x x x x
1 0 0 0 0 0 0 0 0 x x x x x x
0 0 0 0 0 0 0 0 0 x x x x x x
1 0 0 0 0 0 0 0 0 x x x x x x
0 0 0 0 0 0 0 0 0 x x x x x x
1 0 0 0 0 0 0 0 0 x x x x x x
0 0 0 0 0 0 0 0 0 x x x x x x
1 0 0 0 0 0 0 0 0 x x x x x x
0 0 0 0 0 0 0 0 0 x x x x x x
1 0 0 0 0 0 0 0 0 x x x x x x
0 0 0 0 0 0 0 0 0 x x x x x x
1 0 0 0 0 0 0 0 0 x x x x x x
0 0 0 0 0 0 0 0 0 x x x x x x
1 0 0 0 0 0 0 0 0 x x x x x x
0 0 0 0 0 0 0 0 0 x x x x x x
1 0 0 0 0 0 0 0 0 x x x x x x
0 0 0 0 0 0 0 0 0 x x x x x x
1 0 0 0 0 0 0 0 0 x x x x x x
0 0 0 0 0 0 0 0 0 x x x x x x
1 0 0 0 0 0 0 0 0 x x x x x x
0 0 0 0 0 0 0 0 0 x x x x x x
1 0 0 0 0 0 0 0 0 x x x x x x
0 0 0 0 0 0 0 0 0 x x x x x x
1 0 0 0 0 0 0 0 0 x x x x x x
0 0 0 0 0 0 0 0 0 x x x x x x
1 0 0 0 0 0 0 0 0 x x x x x x
0 0 0 0 0 0 0 0 0 x x x x x x
1 0 0 0 0 0 0 0 0 x x x x x x
0 0 0 0 0 0 0 0 0 x x x x x x
1 0 0 0 0 0 0 0 0 x x x x x x
0 0 0 0 0 0 0 0 0 x x x x x x
1 0 0 0 0 0 0 0 0 x x x x x x
0 0 0 0 0 0 0 0 0 x x x x x x
1 0 0 0 0 0 0 0 0 x x x x x x
0 0 0 0 0 0 0 0 0 x x x x x x
1 0 0 0 0 0 0 0 0 x x x x x x
0 0 0 0 0 0 0 0 0 x x x x x x
1 0 0 0 0 0 0 0 0 x x x x x x
0 0 0 0 0 0 0 0 0 0 0 0 1 0 0
1 0 0 0 0 0 0 0 0 0 0 0 1 0 0
0 0 0 1 0 0 0 0 0 0 0 0 1 0 0
1 0 0 1 0 0 0 0 0 0 0 0 1 0 0
0 0 0 0 0 0 0 0 0 x x x x x x
1 0 0 0 0 0 0 0 0 x x x x x x
0 0 0 0 0 0 0 0 0 x x x x x x
1 0 0 0 0 0 0 0 0 x x x x x x
0 0 0 0 0 0 0 0 0 x x x x x x
1 0 0 0 0 0 0 0 0 x x x x x x
0 0 0 0 0 0 0 0 0 x x x x x x
1 0 0 0 0 0 0 0 0 x x x x x x
0 0 0 0 0 0 0 0 0 x x x x x x
1 0 0 0 0 0 0 0 0 x x x x x x
0 0 0 0 0 0 0 0 0 x x x x x x
1 0 0 0 0 0 0 0 0 x x x x x x
0 0 0 0 0 0 0 0 0 x x x x x x
1 0 0 0 0 0 0 0 0 x x x x x x
0 0 0 0 0 0 0 0 0 x x x x x x
1 0 0 0 0 0 0 0 0 x x x x x x
0 0 0 0 0 0 0 0 0 x x x x x x
1 0 0 0 0 0 0 0 0 x x x x x x
0 0 0 0 0 0 0 0 0 x x x x x x
1 0 0 0 0 0 0 0 0 x x x x x x
0 0 0 0 0 0 0 0 0 x x x x x x
1 0 0 0 0 0 0 0 0 x x x x x x
0 0 0 0 0 0 0 0 0 x x x x x x
1 0 0 0 0 0 0 0 0 x x x x x x
0 0 0 0 0 0 0 0 0 x x x x x x
1 0 0 0 0 0 0 0 0 x x x x x x
0 0 0 0 0 0 0 0 0 x x x x x x
1 0 0 0 0 0 0 0 0 x x x x x x
0 0 0 0 0 0 0 0 0 x x x x x x
1 0 0 0 0 0 0 0 0 x x x x x x
0 0 0 0 0 0 0 0 0 x x x x x x
1 0 0 0 0 0 0 0 0 x x x x x x
0 0 0 0 0 0 0 0 0 x x x x x x
1 0 0 0 0 0 0 0 0 x x x x x x
0 0 0 0 0 0 0 0 0 x x x x x x
1 0 0 0 0 0 0 0 0 x x x x x x
0 0 0 0 0 0 0 0 0 x x x x x x
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*/

/* Test case test 4:
clock reset P5 P10 P20 Pcoffee Ptea Pchange Pnext Balance CoffeeOut TeaOut Change5 Change10 Change20
0 1 0 0 0 0 0 0 0 x x x x x x
1 1 0 0 0 0 0 0 0 0 0 0 0 0 0
0 0 0 0 1 0 0 0 0 0 0 0 0 0 0
1 0 0 0 1 0 0 0 0 0 0 0 0 0 0
0 0 0 0 0 0 0 0 0 x x x x x x
1 0 0 0 0 0 0 0 0 x x x x x x
0 0 0 0 0 0 0 0 0 x x x x x x
1 0 0 0 0 0 0 0 0 x x x x x x
0 0 0 0 0 0 0 0 0 x x x x x x
1 0 0 0 0 0 0 0 0 x x x x x x
0 0 0 0 0 0 0 0 0 x x x x x x
1 0 0 0 0 0 0 0 0 x x x x x x
0 0 0 0 0 0 0 0 0 x x x x x x
1 0 0 0 0 0 0 0 0 x x x x x x
0 0 0 0 0 0 0 0 0 x x x x x x
1 0 0 0 0 0 0 0 0 x x x x x x
0 0 0 0 0 0 0 0 0 x x x x x x
1 0 0 0 0 0 0 0 0 x x x x x x
0 0 0 0 0 0 0 0 0 x x x x x x
1 0 0 0 0 0 0 0 0 x x x x x x
0 0 0 0 0 0 0 0 0 x x x x x x
1 0 0 0 0 0 0 0 0 x x x x x x
0 0 0 0 0 0 0 0 0 x x x x x x
1 0 0 0 0 0 0 0 0 x x x x x x
0 0 0 0 0 0 0 0 0 x x x x x x
1 0 0 0 0 0 0 0 0 x x x x x x
0 0 0 0 0 0 0 0 0 x x x x x x
1 0 0 0 0 0 0 0 0 x x x x x x
0 0 0 0 0 0 0 0 0 x x x x x x
1 0 0 0 0 0 0 0 0 x x x x x x
0 0 0 0 0 0 0 0 0 x x x x x x
1 0 0 0 0 0 0 0 0 x x x x x x
0 0 0 0 0 0 0 0 0 x x x x x x
1 0 0 0 0 0 0 0 0 x x x x x x
0 0 0 0 0 0 0 0 0 x x x x x x
1 0 0 0 0 0 0 0 0 x x x x x x
0 0 0 0 0 0 0 0 0 x x x x x x
1 0 0 0 0 0 0 0 0 x x x x x x
0 0 0 0 0 0 0 0 0 x x x x x x
1 0 0 0 0 0 0 0 0 x x x x x x
0 0 0 0 0 0 0 0 0 x x x x x x
1 0 0 0 0 0 0 0 0 x x x x x x
0 0 0 0 0 0 0 0 0 x x x x x x
1 0 0 0 0 0 0 0 0 x x x x x x
0 0 0 0 0 0 0 0 0 20 0 0 0 0 0
1 0 0 0 0 0 0 0 0 20 0 0 0 0 0
0 0 0 0 1 0 0 0 0 20 0 0 0 0 0
1 0 0 0 1 0 0 0 0 20 0 0 0 0 0
0 0 0 0 0 0 0 0 0 x x x x x x
1 0 0 0 0 0 0 0 0 x x x x x x
0 0 0 0 0 0 0 0 0 x x x x x x
1 0 0 0 0 0 0 0 0 x x x x x x
0 0 0 0 0 0 0 0 0 x x x x x x
1 0 0 0 0 0 0 0 0 x x x x x x
0 0 0 0 0 0 0 0 0 x x x x x x
1 0 0 0 0 0 0 0 0 x x x x x x
0 0 0 0 0 0 0 0 0 x x x x x x
1 0 0 0 0 0 0 0 0 x x x x x x
0 0 0 0 0 0 0 0 0 x x x x x x
1 0 0 0 0 0 0 0 0 x x x x x x
0 0 0 0 0 0 0 0 0 x x x x x x
1 0 0 0 0 0 0 0 0 x x x x x x
0 0 0 0 0 0 0 0 0 x x x x x x
1 0 0 0 0 0 0 0 0 x x x x x x
0 0 0 0 0 0 0 0 0 x x x x x x
1 0 0 0 0 0 0 0 0 x x x x x x
0 0 0 0 0 0 0 0 0 x x x x x x
1 0 0 0 0 0 0 0 0 x x x x x x
0 0 0 0 0 0 0 0 0 x x x x x x
1 0 0 0 0 0 0 0 0 x x x x x x
0 0 0 0 0 0 0 0 0 x x x x x x
1 0 0 0 0 0 0 0 0 x x x x x x
0 0 0 0 0 0 0 0 0 x x x x x x
1 0 0 0 0 0 0 0 0 x x x x x x
0 0 0 0 0 0 0 0 0 x x x x x x
1 0 0 0 0 0 0 0 0 x x x x x x
0 0 0 0 0 0 0 0 0 x x x x x x
1 0 0 0 0 0 0 0 0 x x x x x x
0 0 0 0 0 0 0 0 0 x x x x x x
1 0 0 0 0 0 0 0 0 x x x x x x
0 0 0 0 0 0 0 0 0 x x x x x x
1 0 0 0 0 0 0 0 0 x x x x x x
0 0 0 0 0 0 0 0 0 x x x x x x
1 0 0 0 0 0 0 0 0 x x x x x x
0 0 0 0 0 0 0 0 0 x x x x x x
1 0 0 0 0 0 0 0 0 x x x x x x
0 0 0 0 0 0 0 0 0 x x x x x x
1 0 0 0 0 0 0 0 0 x x x x x x
0 0 0 0 0 0 0 0 0 40 0 0 0 0 0
1 0 0 0 0 0 0 0 0 40 0 0 0 0 0
0 0 0 0 0 0 1 0 0 40 0 0 0 0 0
1 0 0 0 0 0 1 0 0 40 0 0 0 0 0
0 0 0 0 0 0 0 0 0 x x x x x x
1 0 0 0 0 0 0 0 0 x x x x x x
0 0 0 0 0 0 0 0 0 x x x x x x
1 0 0 0 0 0 0 0 0 x x x x x x
0 0 0 0 0 0 0 0 0 x x x x x x
1 0 0 0 0 0 0 0 0 x x x x x x
0 0 0 0 0 0 0 0 0 x x x x x x
1 0 0 0 0 0 0 0 0 x x x x x x
0 0 0 0 0 0 0 0 0 x x x x x x
1 0 0 0 0 0 0 0 0 x x x x x x
0 0 0 0 0 0 0 0 0 x x x x x x
1 0 0 0 0 0 0 0 0 x x x x x x
0 0 0 0 0 0 0 0 0 x x x x x x
1 0 0 0 0 0 0 0 0 x x x x x x
0 0 0 0 0 0 0 0 0 x x x x x x
1 0 0 0 0 0 0 0 0 x x x x x x
0 0 0 0 0 0 0 0 0 x x x x x x
1 0 0 0 0 0 0 0 0 x x x x x x
0 0 0 0 0 0 0 0 0 x x x x x x
1 0 0 0 0 0 0 0 0 x x x x x x
0 0 0 0 0 0 0 0 0 x x x x x x
1 0 0 0 0 0 0 0 0 x x x x x x
0 0 0 0 0 0 0 0 0 x x x x x x
1 0 0 0 0 0 0 0 0 x x x x x x
0 0 0 0 0 0 0 0 0 x x x x x x
1 0 0 0 0 0 0 0 0 x x x x x x
0 0 0 0 0 0 0 0 0 x x x x x x
1 0 0 0 0 0 0 0 0 x x x x x x
0 0 0 0 0 0 0 0 0 x x x x x x
1 0 0 0 0 0 0 0 0 x x x x x x
0 0 0 0 0 0 0 0 0 x x x x x x
1 0 0 0 0 0 0 0 0 x x x x x x
0 0 0 0 0 0 0 0 0 x x x x x x
1 0 0 0 0 0 0 0 0 x x x x x x
0 0 0 0 0 0 0 0 0 x x x x x x
1 0 0 0 0 0 0 0 0 x x x x x x
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*/
