// Digital circuit hof09_4.dig as structural Verilog
module hof09_4 (
  input  P5,
  input  reset,
  input  clock,
  input  P10,
  input  P20,
  input  Pcoffee,
  input  Ptea,
  input  Pchange,
  input  Pnext,
  output [5:0] Balance,
  output CoffeeOut,
  output TeaOut,
  output [1:0] Change5,
  output [1:0] Change10,
  output [1:0] Change20
);

  wire CO_plus_TO, comparator_1_lt, comparator_2_lt, comparator_3_lt, comparator_4_gt, comparator_5_gt,
       d_ff_1_q, d_ff_2_q, d_ff_3_q, d_ff_4_q, d_ff_5_q, d_ff_6_q, d_ff_7_q, d_ff_8_nq, d_ff_9_nq,
       d_ff_10_nq, d_ff_11_nq, d_ff_12_nq, d_ff_13_nq, d_ff_14_nq, or_1_out, or_2_out, P5_t, P10_t, P20_t,
       Pch__plus__re, Pch__plus__re__plus__Pn, PChange_t, PCoffee_t, Pnext_t, PTea_t;
  wire [5:0] add_1_s, and_1_out, div_1_q, div_1_r, div_2_q, div_3_q, div_3_r, lookuptable_1_out,
       multiplexer_1_out, multiplexer_2_out, multiplexer_3_out, multiplexer_4_out;
  wire [5:2] register_4_q, register_5_q, register_6_q;

  LookUpTable #(.Bits(6)) lookuptable_1 (
    .in0(P5_t), .in1(P10_t), .in2(P20_t), .in3(PCoffee_t), .in4(PTea_t), .out(lookuptable_1_out));
  Register #(.Bits(6)) register_1 (.D(and_1_out), .C(clock), .en(1'b1), .Q(Balance));
  Register register_2 (.D(PCoffee_t), .C(clock), .en(or_1_out), .Q(CoffeeOut));
  or or_1 (or_1_out, PCoffee_t, Pch__plus__re__plus__Pn);
  Register register_3 (.D(PTea_t), .C(clock), .en(or_2_out), .Q(TeaOut));
  or or_2 (or_2_out, PTea_t, Pch__plus__re__plus__Pn);
  or or_3 (Pch__plus__re__plus__Pn, PChange_t, Pnext_t, reset);
  or or_4 (Pch__plus__re, PChange_t, reset);
  Register #(.Bits(6)) register_4 (.D(multiplexer_1_out), .C(clock), .en(Pch__plus__re), .Q({register_4_q, Change5}));
  Multiplexer #(.Bits(6)) multiplexer_1 (.sel(reset), .in_0(div_2_q), .in_1({6{1'b0}}), .out(multiplexer_1_out));
  Div #(.Bits(6)) div_1 (.a(add_1_s), .b(6'b010100), .q(div_1_q), .r(div_1_r));
  Add #(.Bits(6)) add_1 (.a(Balance), .b(lookuptable_1_out), .c_i(1'b0), .s(add_1_s));  // open: c_o
  assign and_1_out = multiplexer_2_out & add_1_s;  // And and_1, 6 bits wide
  Multiplexer #(.Bits(6)) multiplexer_2 (
    .sel(Pch__plus__re), .in_0({6{1'b1}}), .in_1({6{1'b0}}), .out(multiplexer_2_out));
  Register #(.Bits(6)) register_5 (.D(multiplexer_3_out), .C(clock), .en(Pch__plus__re), .Q({register_5_q, Change10}));
  Div #(.Bits(6)) div_2 (.a(div_3_r), .b(6'b000101), .q(div_2_q));  // open: r
  Multiplexer #(.Bits(6)) multiplexer_3 (.sel(reset), .in_0(div_3_q), .in_1({6{1'b0}}), .out(multiplexer_3_out));
  Multiplexer #(.Bits(6)) multiplexer_4 (.sel(reset), .in_0(div_1_q), .in_1({6{1'b0}}), .out(multiplexer_4_out));
  Div #(.Bits(6)) div_3 (.a(div_1_r), .b(6'b001010), .q(div_3_q), .r(div_3_r));
  Register #(.Bits(6)) register_6 (.D(multiplexer_4_out), .C(clock), .en(Pch__plus__re), .Q({register_6_q, Change20}));
  Comparator #(.Bits(6)) comparator_1 (.a(Balance), .b(6'b101110), .lt(comparator_1_lt));  // open: gt, eq
  Comparator #(.Bits(6)) comparator_2 (.a(Balance), .b(6'b101001), .lt(comparator_2_lt));  // open: gt, eq
  Comparator #(.Bits(6)) comparator_3 (.a(Balance), .b(6'b011111), .lt(comparator_3_lt));  // open: gt, eq
  D_FF d_ff_1 (.D(P5), .C(clock), .Q(d_ff_1_q));  // open: nQ
  and and_2 (P5_t, CO_plus_TO, comparator_1_lt, d_ff_1_q, d_ff_8_nq);
  D_FF d_ff_2 (.D(P10), .C(clock), .Q(d_ff_2_q));  // open: nQ
  and and_3 (P10_t, CO_plus_TO, comparator_2_lt, d_ff_2_q, d_ff_9_nq);
  D_FF d_ff_3 (.D(P20), .C(clock), .Q(d_ff_3_q));  // open: nQ
  and and_4 (P20_t, CO_plus_TO, comparator_3_lt, d_ff_3_q, d_ff_10_nq);
  Comparator #(.Bits(6)) comparator_4 (.a(Balance), .b(6'b011000), .gt(comparator_4_gt));  // open: eq, lt
  D_FF d_ff_4 (.D(Pcoffee), .C(clock), .Q(d_ff_4_q));  // open: nQ
  and and_5 (PCoffee_t, CO_plus_TO, comparator_4_gt, d_ff_4_q, d_ff_11_nq);
  Comparator #(.Bits(6)) comparator_5 (.a(Balance), .b(6'b010011), .gt(comparator_5_gt));  // open: eq, lt
  D_FF d_ff_5 (.D(Ptea), .C(clock), .Q(d_ff_5_q));  // open: nQ
  and and_6 (PTea_t, CO_plus_TO, comparator_5_gt, d_ff_5_q, d_ff_12_nq);
  D_FF d_ff_6 (.D(Pchange), .C(clock), .Q(d_ff_6_q));  // open: nQ
  and and_7 (PChange_t, d_ff_6_q, d_ff_13_nq);
  D_FF d_ff_7 (.D(Pnext), .C(clock), .Q(d_ff_7_q));  // open: nQ
  and and_8 (Pnext_t, d_ff_7_q, d_ff_14_nq);
  D_FF d_ff_8 (.D(d_ff_1_q), .C(clock), .nQ(d_ff_8_nq));  // open: Q
  D_FF d_ff_9 (.D(d_ff_2_q), .C(clock), .nQ(d_ff_9_nq));  // open: Q
  D_FF d_ff_10 (.D(d_ff_3_q), .C(clock), .nQ(d_ff_10_nq));  // open: Q
  D_FF d_ff_11 (.D(d_ff_4_q), .C(clock), .nQ(d_ff_11_nq));  // open: Q
  D_FF d_ff_12 (.D(d_ff_5_q), .C(clock), .nQ(d_ff_12_nq));  // open: Q
  D_FF d_ff_13 (.D(d_ff_6_q), .C(clock), .nQ(d_ff_13_nq));  // open: Q
  D_FF d_ff_14 (.D(d_ff_7_q), .C(clock), .nQ(d_ff_14_nq));  // open: Q
  nor nor_1 (CO_plus_TO, CoffeeOut, TeaOut);

  // Other names for the same wires on the sheet: Clk = clock

  // Notes on the sheet:
  //   contents of lookuptable_1 (hex, n*v repeats v):
  //   0,5,a,0,14,0,0,0,27,7*0,2c
endmodule
