// Digital circuit 64_02.dig as structural Verilog
module _64_02 (
  input  S0,
  input  S1,
  input  S2,
  output O1,
  output O2
);

  wire and_1_out, and_2_out, and_3_out, not_1_out, not_2_out, not_3_out;

  not not_1 (not_1_out, S0);
  not not_2 (not_2_out, S1);
  not not_3 (not_3_out, S2);
  and and_1 (and_1_out, S0, not_2_out);
  and and_2 (and_2_out, S1, not_3_out);
  and and_3 (and_3_out, S0, S1);
  or or_1 (O1, and_1_out, and_2_out);
  or or_2 (O2, and_3_out, not_3_out);
endmodule
