// Digital circuit lab3-01.dig as structural Verilog
module lab3_01 (
  input  [3:0] In,
  input  in_9,
  output A,
  output B,
  output C,
  output D,
  output F,
  output G,
  output E
);

  wire _0, _1, _2, _3, and_1_out, and_2_out, and_3_out, and_4_out, and_5_out, and_6_out, and_7_out,
       and_8_out, and_9_out, and_10_out, and_11_out, and_12_out, and_13_out, and_14_out, and_15_out,
       and_16_out, and_17_out, and_18_out, and_19_out, and_20_out, and_21_out, and_22_out, and_23_out,
       and_24_out, and_25_out, and_26_out, and_27_out;

  not not_1 (_0, In[0]);
  not not_2 (_3, In[3]);
  and and_1 (and_1_out, In[0], In[1], In[2]);
  and and_2 (and_2_out, In[0], _1, In[2]);
  and and_3 (and_3_out, _0, In[1], In[2]);
  and and_4 (and_4_out, _0, _2);
  and and_5 (and_5_out, In[1], _2);
  and and_6 (and_6_out, In[0], In[1], In[2]);
  and and_7 (and_7_out, In[0], _1, In[2]);
  and and_8 (and_8_out, _0, In[1], In[2]);
  and and_9 (and_9_out, _0, _1);
  and and_10 (and_10_out, In[0], _2);
  and and_11 (and_11_out, _0, In[1], In[2]);
  and and_12 (and_12_out, _0, _2);
  and and_13 (and_13_out, _0, In[1], In[2]);
  and and_14 (and_14_out, In[1], _2);
  and and_15 (and_15_out, _1, In[2]);
  not not_3 (_1, In[1]);
  not not_4 (_2, In[2]);
  or or_1 (E, and_11_out, and_12_out);
  or or_2 (A, and_1_out, and_2_out, and_3_out, and_4_out, and_5_out, In[3]);
  or or_3 (C, and_6_out, and_7_out, and_8_out, and_9_out, and_10_out);
  or or_4 (G, and_13_out, and_14_out, and_15_out, In[3]);
  and and_16 (and_16_out, In[0], In[1], In[2]);
  and and_17 (and_17_out, In[0], _2);
  and and_18 (and_18_out, _0, _1);
  and and_19 (and_19_out, _0, _2);
  and and_20 (and_20_out, In[0], _1, In[2]);
  and and_21 (and_21_out, _0, In[1], In[2]);
  and and_22 (and_22_out, _0, _2);
  and and_23 (and_23_out, In[1], _2);
  and and_24 (and_24_out, In[0], _1, In[2]);
  and and_25 (and_25_out, _0, In[1], In[2]);
  and and_26 (and_26_out, _0, _1);
  and and_27 (and_27_out, In[0], In[1], In[2]);
  or or_5 (B, and_16_out, and_17_out, and_18_out, and_19_out);
  or or_6 (D, In[3], and_20_out, and_21_out, and_22_out, and_23_out);
  or or_7 (F, In[3], and_24_out, and_25_out, and_26_out, and_27_out);
  Seven_Seg seven_seg_1 (.a(A), .b(B), .c(C), .d(D), .e(E), .f(F), .g(G), .dp(in_9));

  // Other names for the same wires on the sheet: H = in_9; _0_t = In[0]; _1_t = In[1]; _2_t = In[2]; _3_t = In[3]
endmodule
