// Digital circuit 2020_final_1.dig as structural Verilog
module _2020_final_1 (
  input  [7:0] A,
  input  [7:0] B,
  input  start,
  input  clock,
  output [7:0] output2,
  output busy,
  output [7:0] \output 
);

  wire equal, greater, lesser, start_t;
  wire [7:0] multiplexer_1_out, multiplexer_2_out, multiplexer_3_out, multiplexer_4_out, multiplexer_5_out,
       multiplexer_6_out, sub_1_s, sub_2_s;

  RS_FF_AS rs_ff_as_1 (.S(start), .R(1'b0), .Q(start_t));  // open: nQ
  Sub #(.Bits(8)) sub_1 (.a(\output ), .b(output2), .c_i(1'b0), .s(sub_1_s));  // open: c_o
  Sub #(.Bits(8)) sub_2 (.a(output2), .b(\output ), .c_i(1'b0), .s(sub_2_s));  // open: c_o
  not not_1 (busy, equal);
  Multiplexer #(.Bits(8)) multiplexer_1 (.sel(greater), .in_0(\output ), .in_1(sub_1_s), .out(multiplexer_1_out));
  Multiplexer #(.Bits(8)) multiplexer_2 (.sel(lesser), .in_0(output2), .in_1(sub_2_s), .out(multiplexer_2_out));
  Multiplexer #(.Bits(8)) multiplexer_3 (
    .sel(equal), .in_0(multiplexer_1_out), .in_1(\output ), .out(multiplexer_3_out));
  Multiplexer #(.Bits(8)) multiplexer_4 (
    .sel(equal), .in_0(multiplexer_2_out), .in_1(output2), .out(multiplexer_4_out));
  Multiplexer #(.Bits(8)) multiplexer_5 (.sel(start_t), .in_0(A), .in_1(multiplexer_3_out), .out(multiplexer_5_out));
  Multiplexer #(.Bits(8)) multiplexer_6 (.sel(start_t), .in_0(B), .in_1(multiplexer_4_out), .out(multiplexer_6_out));
  Comparator #(.Bits(8)) comparator_1 (.a(\output ), .b(output2), .gt(greater), .eq(equal), .lt(lesser));
  D_FF #(.Bits(8)) d_ff_1 (.D(multiplexer_5_out), .C(clock), .Q(\output ));  // open: nQ
  D_FF #(.Bits(8)) d_ff_2 (.D(multiplexer_6_out), .C(clock), .Q(output2));  // open: nQ

  // Other names for the same wires on the sheet: A_t[7:0] = \output ; B_t[7:0] = output2
endmodule
