// Digital circuit 2021_final_2.dig as structural Verilog
module _2021_final_2 (
  input  Increase,
  input  clk,
  output [3:0] out_3
);

  wire and_1_out, and_2_out, d_ff_as_1_q, IncreaseSig, MAX, MAX_SYNC;
  wire [3:0] add_1_s, d_ff_as_3_q, multiplexer_1_out;

  D_FF_AS d_ff_as_1 (.Set(1'b0), .D(1'b1), .C(Increase), .Clr(IncreaseSig), .Q(d_ff_as_1_q));  // open: nQ
  Multiplexer #(.Bits(4)) multiplexer_1 (.sel(and_1_out), .in_0(4'b0000), .in_1(4'b0011), .out(multiplexer_1_out));
  and and_1 (and_1_out, IncreaseSig, ~MAX_SYNC);  // And
  D_FF_AS d_ff_as_2 (.Set(1'b0), .D(d_ff_as_1_q), .C(clk), .Clr(1'b0), .Q(IncreaseSig));  // open: nQ
  Add #(.Bits(4)) add_1 (.a(multiplexer_1_out), .b(out_3), .c_i(1'b0), .s(add_1_s));  // open: c_o
  D_FF_AS #(.Bits(4), .Default(3)) d_ff_as_3 (
    .Set(1'b0), .D(add_1_s), .C(clk), .Clr(1'b0), .Q(d_ff_as_3_q));  // open: nQ
  Multiplexer #(.Bits(4)) multiplexer_2 (.sel(and_2_out), .in_0(d_ff_as_3_q), .in_1(4'b0011), .out(out_3));
  and and_2 (and_2_out, IncreaseSig, MAX_SYNC);
  LED led_1 (.in(MAX));
  Seven_Seg_Hex seven_seg_hex_1 (.d(out_3), .dp(1'b0));
  Comparator #(.Bits(4)) comparator_1 (.a(out_3), .b(4'b1111), .eq(MAX));  // open: gt, lt
  D_FF d_ff_1 (.D(MAX), .C(clk), .Q(MAX_SYNC));  // open: nQ

  // Other names for the same wires on the sheet: CurrentCount[3:0] = out_3
endmodule
