// Digital circuit 2557.dig as structural Verilog
module _2557 (
  input  [3:0] Numerator,
  input  [3:0] Denominator,
  output [3:0] Remainder,
  output [3:0] Quotient
);

  wire comparator_1_eq;
  wire [3:0] div_1_q, div_1_r;

  Div #(.Bits(4)) div_1 (.a(Numerator), .b(Denominator), .q(div_1_q), .r(div_1_r));
  Comparator #(.Bits(4)) comparator_1 (.a(Denominator), .b(4'b0000), .eq(comparator_1_eq));  // open: gt, lt
  Multiplexer #(.Bits(4)) multiplexer_1 (.sel(comparator_1_eq), .in_0(div_1_q), .in_1(4'b0000), .out(Quotient));
  Multiplexer #(.Bits(4)) multiplexer_2 (.sel(comparator_1_eq), .in_0(div_1_r), .in_1(4'b0000), .out(Remainder));
endmodule
