// Digital circuit 2558-1.dig as structural Verilog
module _2558_1 (
  input  clk,
  output out_1
);

  wire and_1_out, button_1_out, comparator_1_eq, comparator_2_eq;
  wire [3:0] add_1_s, d_ff_1_q, multiplexer_1_out, multiplexer_2_out;

  Button button_1 (.out(button_1_out));
  Multiplexer #(.Bits(4)) multiplexer_1 (.sel(button_1_out), .in_0(4'b0000), .in_1(4'b0011), .out(multiplexer_1_out));
  Add #(.Bits(4)) add_1 (.a(d_ff_1_q), .b(multiplexer_1_out), .c_i(1'b0), .s(add_1_s));  // open: c_o
  and and_1 (and_1_out, button_1_out, out_1);
  Multiplexer #(.Bits(4)) multiplexer_2 (.sel(and_1_out), .in_0(add_1_s), .in_1(4'b0010), .out(multiplexer_2_out));
  D_FF #(.Bits(4)) d_ff_1 (.D(multiplexer_2_out), .C(clk), .Q(d_ff_1_q));  // open: nQ
  Comparator #(.Bits(4)) comparator_1 (.a(d_ff_1_q), .b(4'b0000), .eq(comparator_1_eq));  // open: gt, lt
  Comparator #(.Bits(4)) comparator_2 (.a(d_ff_1_q), .b(4'b1110), .eq(comparator_2_eq));  // open: gt, lt
  Seven_Seg_Hex seven_seg_hex_1 (.d(d_ff_1_q), .dp(1'b0));
  or or_1 (out_1, comparator_1_eq, comparator_2_eq);
endmodule
