// Digital circuit 2559-1.dig as structural Verilog
module _2559_1 (
  input  clk
);

  wire A, and_1_out, and_2_out, and_3_out, and_4_out, and_5_out, and_6_out, and_7_out, and_8_out, and_9_out,
       and_10_out, B, Beware_out, C, Drive_out, I0, I1, not_1_out, not_2_out, not_3_out, or_3_out, or_4_out,
       or_5_out, Walk_out;
  wire [2:0] lookuptable_1_out, lookuptable_2_out, lookuptable_3_out, lookuptable_4_out, lookuptable_5_out,
       lookuptable_6_out, lookuptable_7_out, lookuptable_8_out, multiplexer_1_out;

  Button Walk (.out(Walk_out));
  or or_1 (I0, Walk_out, Beware_out);
  Button Beware (.out(Beware_out));
  or or_2 (I1, Beware_out, Drive_out);
  Button Drive (.out(Drive_out));
  LookUpTable #(.Bits(3)) lookuptable_1 (.in0(I0), .in1(I1), .out(lookuptable_1_out));
  LookUpTable #(.Bits(3)) lookuptable_2 (.in0(I0), .in1(I1), .out(lookuptable_2_out));
  LookUpTable #(.Bits(3)) lookuptable_3 (.in0(I0), .in1(I1), .out(lookuptable_3_out));
  LookUpTable #(.Bits(3)) lookuptable_4 (.in0(I0), .in1(I1), .out(lookuptable_4_out));
  LookUpTable #(.Bits(3)) lookuptable_5 (.in0(I0), .in1(I1), .out(lookuptable_5_out));
  LookUpTable #(.Bits(3)) lookuptable_6 (.in0(I0), .in1(I1), .out(lookuptable_6_out));
  LookUpTable #(.Bits(3)) lookuptable_7 (.in0(I0), .in1(I1), .out(lookuptable_7_out));
  LookUpTable #(.Bits(3)) lookuptable_8 (.in0(I0), .in1(I1), .out(lookuptable_8_out));
  Multiplexer #(.Bits(3), .Selector_Bits(3)) multiplexer_1 (
    .sel({C, B, A}), .in_0(lookuptable_1_out), .in_1(lookuptable_2_out), .in_2(lookuptable_3_out),
    .in_3(lookuptable_4_out), .in_4(lookuptable_5_out), .in_5(lookuptable_6_out), .in_6(lookuptable_7_out),
    .in_7(lookuptable_8_out), .out(multiplexer_1_out));
  D_FF_AS #(.Bits(3)) d_ff_as_1 (.Set(1'b0), .D(multiplexer_1_out), .C(clk), .Clr(1'b0), .Q({C, B, A}));  // open: nQ
  not not_1 (not_1_out, C);
  not not_2 (not_2_out, B);
  not not_3 (not_3_out, A);
  and and_1 (and_1_out, not_1_out, not_2_out, A);
  and and_2 (and_2_out, not_1_out, B, A);
  and and_3 (and_3_out, C, not_2_out, A);
  and and_4 (and_4_out, C, not_3_out);
  and and_5 (and_5_out, C, B);
  and and_6 (and_6_out, B, not_3_out);
  and and_7 (and_7_out, not_1_out, B, not_3_out);
  and and_8 (and_8_out, C, not_2_out);
  and and_9 (and_9_out, not_1_out, A);
  and and_10 (and_10_out, C, B);
  or or_3 (or_3_out, and_2_out, and_3_out);
  or or_4 (or_4_out, and_4_out, and_5_out, and_6_out);
  or or_5 (or_5_out, and_9_out, and_10_out);
  LED led_1 (.in(and_1_out));
  LED led_2 (.in(or_3_out));
  LED led_3 (.in(or_4_out));
  LED led_4 (.in(and_7_out));
  LED led_5 (.in(and_8_out));
  LED led_6 (.in(or_5_out));

  // Notes on the sheet:
  //   contents of lookuptable_1 (hex, n*v repeats v):
  //   5,1,2,5
  //   contents of lookuptable_2 (hex, n*v repeats v):
  //   1,1,3
  //   contents of lookuptable_3 (hex, n*v repeats v):
  //   2,4,2
  //   contents of lookuptable_4 (hex, n*v repeats v):
  //   4*7
  //   contents of lookuptable_5 (hex, n*v repeats v):
  //   4*6
  //   contents of lookuptable_6 (hex, n*v repeats v):
  //   0,1,2
  //   contents of lookuptable_7 (hex, n*v repeats v):
  //   4*1
  //   contents of lookuptable_8 (hex, n*v repeats v):
  //   4*2
endmodule
