// Digital circuit 2559-2.dig as structural Verilog
module _2559_2 (
  input  [3:0] in_1
);

  wire [7:0] mul_1_mul;

  Mul #(.Bits(4)) mul_1 (.a(in_1), .b(4'b1001), .mul(mul_1_mul));
  Seven_Seg_Hex seven_seg_hex_1 (.d(mul_1_mul[7:4]), .dp(1'b0));
  Seven_Seg_Hex seven_seg_hex_2 (.d(mul_1_mul[3:0]), .dp(1'b0));
endmodule
