// Digital circuit 2563-1.dig as structural Verilog
module _2563_1 (
  input  [7:0] A,
  input  [7:0] B,
  input  Start,
  input  clk,
  output Busy,
  output [7:0] \output 
);

  wire and_1_out, comparator_1_eq, comparator_2_eq;
  wire [7:0] counter_1_out, div_1_r, div_2_r;

  and and_1 (and_1_out, Busy, Start);
  Counter #(.Bits(8)) counter_1 (.en(and_1_out), .C(clk), .clr(~Start), .out(counter_1_out));  // open: ovf
  Sub #(.Bits(8)) sub_1 (.a({8{1'b1}}), .b(counter_1_out), .c_i(1'b0), .s(\output ));  // open: c_o
  Div #(.Bits(8)) div_1 (.a(A), .b(\output ), .r(div_1_r));  // open: q
  Div #(.Bits(8)) div_2 (.a(B), .b(\output ), .r(div_2_r));  // open: q
  Comparator #(.Bits(8)) comparator_1 (.a({8{1'b0}}), .b(div_1_r), .eq(comparator_1_eq));  // open: gt, lt
  Comparator #(.Bits(8)) comparator_2 (.a({8{1'b0}}), .b(div_2_r), .eq(comparator_2_eq));  // open: gt, lt
  nand nand_1 (Busy, comparator_1_eq, comparator_2_eq);

  // Notes on the sheet:
  //   clk: Hz: 2147483647
endmodule
