// Digital circuit 2564-1.dig as structural Verilog
module _2564_1 (
  input  [7:0] A,
  input  Add,
  input  clk
);

  wire and_1_out, d_ff_1_nq, d_ff_2_q;
  wire [3:0] d_ff_3_q, d_ff_3_q_2, d_ff_3_q_3;
  wire [7:0] multiplexer_1_out;
  wire [11:0] add_1_s;

  Multiplexer #(.Bits(8)) multiplexer_1 (.sel(d_ff_2_q), .in_0({8{1'b0}}), .in_1(A), .out(multiplexer_1_out));
  D_FF d_ff_1 (.D(Add), .C(clk), .nQ(d_ff_1_nq));  // open: Q
  and and_1 (and_1_out, Add, d_ff_1_nq);
  D_FF d_ff_2 (.D(and_1_out), .C(clk), .Q(d_ff_2_q));  // open: nQ
  Add #(.Bits(12)) add_1 (
    .a({d_ff_3_q_3, d_ff_3_q_2, d_ff_3_q}), .b({4'b0000, multiplexer_1_out}), .c_i(1'b0), .s(add_1_s));  // open: c_o
  D_FF #(.Bits(12)) d_ff_3 (.D(add_1_s), .C(clk), .Q({d_ff_3_q_3, d_ff_3_q_2, d_ff_3_q}));  // open: nQ
  Seven_Seg_Hex seven_seg_hex_1 (.d(d_ff_3_q_3), .dp(1'b0));
  Seven_Seg_Hex seven_seg_hex_2 (.d(d_ff_3_q_2), .dp(1'b0));
  Seven_Seg_Hex seven_seg_hex_3 (.d(d_ff_3_q), .dp(1'b0));
endmodule
