// Digital circuit 2564-2.dig as structural Verilog
module _2564_2 (
  input  clk,
  output out_2
);

  wire \input ;
  wire [2:0] d_ff_1_q, lookuptable_1_out, lookuptable_2_out, lookuptable_3_out, lookuptable_4_out,
       lookuptable_5_out, multiplexer_1_out;
  wire [3:0] mul_1_mul;
  wire [5:4] mul_1_mul_2;

  Button button_1 (.out(\input ));
  LookUpTable #(.Bits(3)) lookuptable_1 (.in0(\input ), .in1(1'b0), .out(lookuptable_1_out));
  LookUpTable #(.Bits(3)) lookuptable_2 (.in0(\input ), .in1(1'b0), .out(lookuptable_2_out));
  LookUpTable #(.Bits(3)) lookuptable_3 (.in0(\input ), .in1(1'b0), .out(lookuptable_3_out));
  LookUpTable #(.Bits(3)) lookuptable_4 (.in0(\input ), .in1(1'b0), .out(lookuptable_4_out));
  LookUpTable #(.Bits(3)) lookuptable_5 (.in0(\input ), .in1(1'b0), .out(lookuptable_5_out));
  Multiplexer #(.Bits(3), .Selector_Bits(3)) multiplexer_1 (
    .sel(d_ff_1_q), .in_0(3'b001), .in_1(lookuptable_1_out), .in_2(lookuptable_2_out),
    .in_3(lookuptable_3_out), .in_4(lookuptable_4_out), .in_5(lookuptable_5_out), .in_6(3'b001),
    .in_7(3'b001), .out(multiplexer_1_out));
  D_FF #(.Bits(3)) d_ff_1 (.D(multiplexer_1_out), .C(clk), .Q(d_ff_1_q));  // open: nQ
  Mul #(.Bits(3)) mul_1 (.a(d_ff_1_q), .b(3'b011), .mul({mul_1_mul_2, mul_1_mul}));
  Seven_Seg_Hex seven_seg_hex_1 (.d(mul_1_mul), .dp(1'b0));
  Comparator #(.Bits(4)) comparator_1 (.a(mul_1_mul), .b(4'b1111), .eq(out_2));  // open: gt, lt

  // Notes on the sheet:
  //   contents of lookuptable_1 (hex, n*v repeats v):
  //   1,2,1,1
  //   contents of lookuptable_2 (hex, n*v repeats v):
  //   2,3,2,2
  //   contents of lookuptable_3 (hex, n*v repeats v):
  //   3,4,3,3
  //   contents of lookuptable_4 (hex, n*v repeats v):
  //   4,5,4,4
  //   contents of lookuptable_5 (hex, n*v repeats v):
  //   5,1,5,5
endmodule
