// Digital circuit 01.dig as structural Verilog
module _01 (
  input  reset,
  input  clk,
  output A,
  output B,
  output C
);

  wire [2:0] lookuptable_1_out, lookuptable_2_out, lookuptable_3_out, lookuptable_4_out, lookuptable_5_out,
       lookuptable_6_out, lookuptable_7_out, lookuptable_8_out, multiplexer_1_out;

  LookUpTable #(.Bits(3)) lookuptable_1 (.in0(reset), .in1(1'b0), .out(lookuptable_1_out));
  LookUpTable #(.Bits(3)) lookuptable_2 (.in0(reset), .in1(1'b0), .out(lookuptable_2_out));
  LookUpTable #(.Bits(3)) lookuptable_3 (.in0(reset), .in1(1'b0), .out(lookuptable_3_out));
  LookUpTable #(.Bits(3)) lookuptable_4 (.in0(reset), .in1(1'b0), .out(lookuptable_4_out));
  LookUpTable #(.Bits(3)) lookuptable_5 (.in0(reset), .in1(1'b0), .out(lookuptable_5_out));
  LookUpTable #(.Bits(3)) lookuptable_6 (.in0(reset), .in1(1'b0), .out(lookuptable_6_out));
  LookUpTable #(.Bits(3)) lookuptable_7 (.in0(reset), .in1(1'b0), .out(lookuptable_7_out));
  LookUpTable #(.Bits(3)) lookuptable_8 (.in0(reset), .in1(1'b0), .out(lookuptable_8_out));
  Multiplexer #(.Bits(3), .Selector_Bits(3)) multiplexer_1 (
    .sel({C, B, A}), .in_0(lookuptable_1_out), .in_1(lookuptable_2_out), .in_2(lookuptable_3_out),
    .in_3(lookuptable_4_out), .in_4(lookuptable_5_out), .in_5(lookuptable_6_out), .in_6(lookuptable_7_out),
    .in_7(lookuptable_8_out), .out(multiplexer_1_out));
  D_FF #(.Bits(3)) d_ff_1 (.D(multiplexer_1_out), .C(clk), .Q({C, B, A}));  // open: nQ

  // Notes on the sheet:
  //   contents of lookuptable_1 (hex, n*v repeats v):
  //   1
  //   contents of lookuptable_2 (hex, n*v repeats v):
  //   3
  //   contents of lookuptable_3 (hex, n*v repeats v):
  //   6
  //   contents of lookuptable_4 (hex, n*v repeats v):
  //   2
  //   contents of lookuptable_6 (hex, n*v repeats v):
  //   4
  //   contents of lookuptable_7 (hex, n*v repeats v):
  //   7
  //   contents of lookuptable_8 (hex, n*v repeats v):
  //   5
endmodule

/* Test case TestCase:
clk reset C B A
0 0 0 0 0 
0 1 0 0 0
1 1 0 0 0
0 0 0 0 0
1 0 0 0 1
0 0 0 0 1
1 0 0 1 1
0 0 0 1 1
1 0 0 1 0
0 0 0 1 0
1 0 1 1 0
0 0 1 1 0
1 0 1 1 1
0 0 1 1 1
1 0 1 0 1
0 0 1 0 1
1 0 1 0 0
0 0 1 0 0
1 0 0 0 0
0 0 0 0 0
1 0 0 0 1
0 0 0 0 1
1 0 0 1 1
0 0 0 1 1
1 0 0 1 0
0 0 0 1 0
1 0 1 1 0
0 0 1 1 0
1 0 1 1 1
0 0 1 1 1
1 0 1 0 1
0 0 1 0 1
1 0 1 0 0
0 0 1 0 0
*/
