// Digital circuit 02.dig as structural Verilog
module _02 (
  input  [15:0] A,
  input  \input ,
  input  clk,
  output [7:0] sqrt,
  output busy
);

  wire and_1_out, comparator_1_eq, comparator_1_lt, d_ff_1_nq, done, or_1_out, or_2_out, s;
  wire [7:0] counter_1_out, sub_1_s;
  wire [15:0] mul_1_mul;

  D_FF d_ff_1 (.D(\input ), .C(clk), .nQ(d_ff_1_nq));  // open: Q
  Counter #(.Bits(8)) counter_1 (.en(busy), .C(clk), .clr(s), .out(counter_1_out));  // open: ovf
  or or_1 (or_1_out, \input , busy);
  and and_1 (and_1_out, \input , d_ff_1_nq);
  Sub #(.Bits(8)) sub_1 (.a({8{1'b1}}), .b(counter_1_out), .c_i(1'b0), .s(sub_1_s));  // open: c_o
  and and_2 (busy, or_1_out, ~done);  // And
  D_FF d_ff_2 (.D(and_1_out), .C(clk), .Q(s));  // open: nQ
  Register #(.Bits(8)) register_1 (.D(sub_1_s), .C(clk), .en(done), .Q(sqrt));
  Mul #(.Bits(8)) mul_1 (.a(sub_1_s), .b(sub_1_s), .mul(mul_1_mul));
  Comparator #(.Bits(16)) comparator_1 (.a(mul_1_mul), .b(A), .eq(comparator_1_eq), .lt(comparator_1_lt));  // open: gt
  or or_2 (or_2_out, comparator_1_eq, comparator_1_lt);
  and and_3 (done, or_2_out, ~s);  // And

  // Notes on the sheet:
  //   clk: Hz: 100
endmodule

/* Test case TestCase1:
clk A input sqrt busy
0 0 0 0 0
1 0 0 0 0
0 0 0 0 0
1 0 0 0 0
0 0 1 X X
1 0 1 X X
loop(x,1000)
0 0 0 X X
1 0 0 X X
end loop
0 0 0 0 0
1 0 0 0 0
*/

/* Test case TestCase2:
clk A input sqrt busy
0 0 0 0 0
1 0 0 0 0
0 0 0 0 0
1 0 0 0 0
0 1 1 X X
1 1 1 X X
loop(x,1000)
0 1 0 X X
1 1 0 X X
end loop
0 0 0 1 0
1 0 0 1 0
*/

/* Test case TestCase3:
clk A input sqrt busy
0 0 0 0 0
1 0 0 0 0
0 0 0 0 0
1 0 0 0 0
0 4 1 X X
1 4 1 X X
loop(x,1000)
0 4 0 X X
1 4 0 X X
end loop
0 0 0 2 0
1 0 0 2 0
*/

/* Test case TestCase4:
clk A input sqrt busy
0 0 0 0 0
1 0 0 0 0
0 0 0 0 0
1 0 0 0 0
0 9 1 X X
1 9 1 X X
loop(x,1000)
0 9 0 X X
1 9 0 X X
end loop
0 0 0 3 0
1 0 0 3 0
*/

/* Test case TestCase5:
clk A input sqrt busy
0 0 0 0 0
1 0 0 0 0
0 0 0 0 0
1 0 0 0 0
0 8 1 X X
1 8 1 X X
loop(x,1000)
0 8 0 X X
1 8 0 X X
end loop
0 0 0 2 0
1 0 0 2 0
*/
