// Digital circuit 03.dig as structural Verilog
module _03 (
  input  [15:0] A,
  input  \input ,
  input  clk,
  input  reset,
  output [15:0] mean,
  output busy
);

  wire and_1_out, d_ff_1_nq;
  wire [3:0] counter_1_out;
  wire [19:0] add_1_s, d_ff_3_q, multiplexer_1_out;
  wire [19:16] div_1_q;

  D_FF d_ff_1 (.D(\input ), .C(clk), .nQ(d_ff_1_nq));  // open: Q
  and and_1 (and_1_out, \input , d_ff_1_nq);
  D_FF d_ff_2 (.D(and_1_out), .C(clk), .Q(busy));  // open: nQ
  Multiplexer #(.Bits(20)) multiplexer_1 (.sel(busy), .in_0({20{1'b0}}), .in_1({4'b0000, A}), .out(multiplexer_1_out));
  Add #(.Bits(20)) add_1 (.a(d_ff_3_q), .b(multiplexer_1_out), .c_i(1'b0), .s(add_1_s));  // open: c_o
  Counter #(.Bits(4)) counter_1 (.en(busy), .C(clk), .clr(reset), .out(counter_1_out));  // open: ovf
  D_FF #(.Bits(20)) d_ff_3 (.D(add_1_s), .C(clk), .Q(d_ff_3_q));  // open: nQ
  Div #(.Bits(20)) div_1 (.a(d_ff_3_q), .b({{16{1'b0}}, counter_1_out}), .q({div_1_q, mean}));  // open: r

  // Other names for the same wires on the sheet: s = busy
endmodule

/* Test case Case1:
clk A input reset mean busy
0 0 0 0 0 0
1 0 0 0 0 0
0 0 0 1 0 0
1 0 0 1 0 0
0 0 0 0 0 0
1 0 0 0 0 0
0 5 1 0 X X
1 5 1 0 X X
0 5 0 0 X X
1 5 0 0 X X
loop(x,500)
end loop
0 0 0 0 5 0
1 0 0 0 5 0
*/

/* Test case Case2:
clk A input reset mean busy
0 0 0 0 0 0
1 0 0 0 0 0
0 0 0 1 0 0
1 0 0 1 0 0
0 0 0 0 0 0
1 0 0 0 0 0
0 5 1 0 X X
1 5 1 0 X X
0 5 0 0 X X
1 5 0 0 X X
loop(x,500)
end loop
0 0 0 0 5 0
1 0 0 0 5 0
0 15 1 0 X X
1 15 1 0 X X
0 15 0 0 X X
1 15 0 0 X X
loop(x,500)
end loop
0 0 0 0 10 0
1 0 0 0 10 0
*/

/* Test case Case3:
clk A input reset mean busy
0 0 0 0 0 0
1 0 0 0 0 0
0 0 0 1 0 0
1 0 0 1 0 0
0 0 0 0 0 0
1 0 0 0 0 0
0 65535 1 0 X X
1 65535 1 0 X X
0 65535 0 0 X X
1 65535 0 0 X X
loop(x,500)
end loop
0 0 0 0 65535 0
1 0 0 0 65535 0
0 65535 1 0 X X
1 65535 1 0 X X
0 65535 0 0 X X
1 65535 0 0 X X
loop(x,500)
end loop
0 0 0 0 65535 0
1 0 0 0 65535 0
*/

/* Test case Case4:
clk A input reset mean busy
0 0 0 0 0 0
1 0 0 0 0 0
0 0 0 1 0 0
1 0 0 1 0 0
0 0 0 0 0 0
1 0 0 0 0 0
0 1 1 0 X X
1 1 1 0 X X
0 1 0 0 X X
1 1 0 0 X X
loop(x,500)
end loop
0 0 0 0 1 0
1 0 0 0 1 0
0 2 1 0 X X
1 2 1 0 X X
0 2 0 0 X X
1 2 0 0 X X
loop(x,500)
end loop
0 0 0 0 1 0
1 0 0 0 1 0
0 3 1 0 X X
1 3 1 0 X X
0 3 0 0 X X
1 3 0 0 X X
loop(x,500)
end loop
0 0 0 0 2 0
1 0 0 0 2 0
0 4 1 0 X X
1 4 1 0 X X
0 4 0 0 X X
1 4 0 0 X X
loop(x,500)
end loop
0 0 0 0 2 0
1 0 0 0 2 0
0 5 1 0 X X
1 5 1 0 X X
0 5 0 0 X X
1 5 0 0 X X
loop(x,500)
end loop
0 0 0 0 3 0
1 0 0 0 3 0
0 6 1 0 X X
1 6 1 0 X X
0 6 0 0 X X
1 6 0 0 X X
loop(x,500)
end loop
0 0 0 0 3 0
1 0 0 0 3 0
0 7 1 0 X X
1 7 1 0 X X
0 7 0 0 X X
1 7 0 0 X X
loop(x,500)
end loop
0 0 0 0 4 0
1 0 0 0 4 0
0 8 1 0 X X
1 8 1 0 X X
0 8 0 0 X X
1 8 0 0 X X
loop(x,500)
end loop
0 0 0 0 4 0
1 0 0 0 4 0
0 9 1 0 X X
1 9 1 0 X X
0 9 0 0 X X
1 9 0 0 X X
loop(x,500)
end loop
0 0 0 0 5 0
1 0 0 0 5 0
0 10 1 0 X X
1 10 1 0 X X
0 10 0 0 X X
1 10 0 0 X X
loop(x,500)
end loop
0 0 0 0 5 0
1 0 0 0 5 0
0 11 1 0 X X
1 11 1 0 X X
0 11 0 0 X X
1 11 0 0 X X
loop(x,500)
end loop
0 0 0 0 6 0
1 0 0 0 6 0
0 12 1 0 X X
1 12 1 0 X X
0 12 0 0 X X
1 12 0 0 X X
loop(x,500)
end loop
0 0 0 0 6 0
1 0 0 0 6 0
0 13 1 0 X X
1 13 1 0 X X
0 13 0 0 X X
1 13 0 0 X X
loop(x,500)
end loop
0 0 0 0 7 0
1 0 0 0 7 0
0 14 1 0 X X
1 14 1 0 X X
0 14 0 0 X X
1 14 0 0 X X
loop(x,500)
end loop
0 0 0 0 7 0
1 0 0 0 7 0
0 15 1 0 X X
1 15 1 0 X X
0 15 0 0 X X
1 15 0 0 X X
loop(x,500)
end loop
0 0 0 0 8 0
1 0 0 0 8 0
*/

/* Test case Case5:
clk A input reset mean busy
0 0 0 0 0 0
1 0 0 0 0 0
0 0 0 1 0 0
1 0 0 1 0 0
0 0 0 0 0 0
1 0 0 0 0 0
0 0 1 0 X X
1 0 1 0 X X
0 0 0 0 X X
1 0 0 0 X X
loop(x,500)
end loop
0 0 0 0 0 0
1 0 0 0 0 0
0 0 1 0 X X
1 0 1 0 X X
0 0 0 0 X X
1 0 0 0 X X
loop(x,500)
end loop
0 0 0 0 0 0
1 0 0 0 0 0
0 0 1 0 X X
1 0 1 0 X X
0 0 0 0 X X
1 0 0 0 X X
loop(x,500)
end loop
0 0 0 0 0 0
1 0 0 0 0 0
0 0 1 0 X X
1 0 1 0 X X
0 0 0 0 X X
1 0 0 0 X X
loop(x,500)
end loop
0 0 0 0 0 0
1 0 0 0 0 0
0 0 1 0 X X
1 0 1 0 X X
0 0 0 0 X X
1 0 0 0 X X
loop(x,500)
end loop
0 0 0 0 0 0
1 0 0 0 0 0
0 0 1 0 X X
1 0 1 0 X X
0 0 0 0 X X
1 0 0 0 X X
loop(x,500)
end loop
0 0 0 0 0 0
1 0 0 0 0 0
0 0 1 0 X X
1 0 1 0 X X
0 0 0 0 X X
1 0 0 0 X X
loop(x,500)
end loop
0 0 0 0 0 0
1 0 0 0 0 0
0 0 1 0 X X
1 0 1 0 X X
0 0 0 0 X X
1 0 0 0 X X
loop(x,500)
end loop
0 0 0 0 0 0
1 0 0 0 0 0
0 0 1 0 X X
1 0 1 0 X X
0 0 0 0 X X
1 0 0 0 X X
loop(x,500)
end loop
0 0 0 0 0 0
1 0 0 0 0 0
0 0 1 0 X X
1 0 1 0 X X
0 0 0 0 X X
1 0 0 0 X X
loop(x,500)
end loop
0 0 0 0 0 0
1 0 0 0 0 0
*/
