// Digital circuit 01.dig as structural Verilog
module _01 (
  input  clk,
  input  reset,
  output A,
  output B,
  output C,
  output [2:0] out_6
);

  wire and_1_out, and_2_out, and_3_out, and_4_out, and_5_out, and_6_out, not_1_out, not_3_out, not_5_out,
       not_6_out, or_1_out, or_3_out, or_5_out;

  not not_1 (not_1_out, reset);
  not not_2 (not_1_out, reset);
  not not_3 (not_3_out, C);
  not not_4 (not_3_out, C);
  not not_5 (not_5_out, B);
  not not_6 (not_6_out, A);
  not not_7 (not_5_out, B);
  not not_8 (not_6_out, A);
  and and_1 (and_1_out, not_6_out, B, not_1_out);
  and and_2 (and_2_out, A, C, not_1_out);
  and and_3 (and_3_out, A, not_3_out, not_1_out);
  and and_4 (and_4_out, not_6_out, B, not_1_out);
  and and_5 (and_5_out, not_5_out, not_3_out, not_1_out);
  and and_6 (and_6_out, B, C, not_1_out);
  or or_1 (or_1_out, and_1_out, and_2_out);
  or or_2 (or_1_out, and_1_out, and_2_out);
  or or_3 (or_3_out, and_3_out, and_4_out);
  or or_4 (or_3_out, and_3_out, and_4_out);
  or or_5 (or_5_out, and_5_out, and_6_out);
  D_FF Z_2_n (.D(or_1_out), .C(clk), .Q(C));  // open: nQ
  D_FF Z_1_n (.D(or_3_out), .C(clk), .Q(B));  // open: nQ
  D_FF Z_0_n (.D(or_5_out), .C(clk), .Q(A));  // open: nQ

  assign out_6 = {C, B, A};
endmodule

/* Test case TestCase:
clk reset C B A
0 0 0 0 0 
0 1 0 0 0
1 1 0 0 0
0 0 0 0 0
1 0 0 0 1
0 0 0 0 1
1 0 0 1 1
0 0 0 1 1
1 0 0 1 0
0 0 0 1 0
1 0 1 1 0
0 0 1 1 0
1 0 1 1 1
0 0 1 1 1
1 0 1 0 1
0 0 1 0 1
1 0 1 0 0
0 0 1 0 0
1 0 0 0 0
0 0 0 0 0
1 0 0 0 1
0 0 0 0 1
1 0 0 1 1
0 0 0 1 1
1 0 0 1 0
0 0 0 1 0
1 0 1 1 0
0 0 1 1 0
1 0 1 1 1
0 0 1 1 1
1 0 1 0 1
0 0 1 0 1
1 0 1 0 0
0 0 1 0 0
*/
