// Digital circuit 02.dig as structural Verilog
module _02 (
  input  [15:0] A,
  input  \input ,
  input  clk,
  output [7:0] sqrt,
  output busy
);

  wire and_1_out, input_t;
  wire [7:0] add_1_s, multiplexer_1_out;
  wire [15:0] mul_1_mul;

  RS_FF_AS rs_ff_as_1 (.S(\input ), .R(1'b0), .Q(input_t));  // open: nQ
  Mul #(.Bits(8)) mul_1 (.a(sqrt), .b(sqrt), .mul(mul_1_mul));
  Comparator #(.Bits(16)) comparator_1 (.a(mul_1_mul), .b(A), .lt(busy));  // open: gt, eq
  Add #(.Bits(8)) add_1 (.a(sqrt), .b({8{1'b0}}), .c_i(1'b1), .s(add_1_s));  // open: c_o
  and and_1 (and_1_out, input_t, busy);
  Multiplexer #(.Bits(8)) multiplexer_1 (.sel(and_1_out), .in_0(sqrt), .in_1(add_1_s), .out(multiplexer_1_out));
  D_FF #(.Bits(8)) d_ff_1 (.D(multiplexer_1_out), .C(clk), .Q(sqrt));  // open: nQ

  // Notes on the sheet:
  //   clk: Hz: 200
endmodule

/* Test case TestCase1:
clk A input sqrt busy
0 0 0 0 0
1 0 0 0 0
0 0 0 0 0
1 0 0 0 0
0 0 1 X X
1 0 1 X X
loop(x,1000)
0 0 0 X X
1 0 0 X X
end loop
0 0 0 0 0
1 0 0 0 0
*/

/* Test case TestCase2:
clk A input sqrt busy
0 0 0 0 0
1 0 0 0 0
0 0 0 0 0
1 0 0 0 0
0 1 1 X X
1 1 1 X X
loop(x,1000)
0 1 0 X X
1 1 0 X X
end loop
0 0 0 1 0
1 0 0 1 0
*/

/* Test case TestCase3:
clk A input sqrt busy
0 0 0 0 0
1 0 0 0 0
0 0 0 0 0
1 0 0 0 0
0 4 1 X X
1 4 1 X X
loop(x,1000)
0 4 0 X X
1 4 0 X X
end loop
0 0 0 2 0
1 0 0 2 0
*/

/* Test case TestCase4:
clk A input sqrt busy
0 0 0 0 0
1 0 0 0 0
0 0 0 0 0
1 0 0 0 0
0 9 1 X X
1 9 1 X X
loop(x,1000)
0 9 0 X X
1 9 0 X X
end loop
0 0 0 3 0
1 0 0 3 0
*/

/* Test case TestCase5:
clk A input sqrt busy
0 0 0 0 0
1 0 0 0 0
0 0 0 0 0
1 0 0 0 0
0 8 1 X X
1 8 1 X X
loop(x,1000)
0 8 0 X X
1 8 0 X X
end loop
0 0 0 2 0
1 0 0 2 0
*/
