// Digital circuit RYG.dig as structural Verilog
module RYG (
  input  Warning,
  input  Human,
  input  Car,
  input  clk
);

  wire and_1_out, and_2_out, and_3_out, and_4_out, C0, c0_t, C01, C1, c1_t, C3, decoder_1_out_1,
       decoder_1_out_2, decoder_1_out_3, decoder_2_out_1, decoder_2_out_2, decoder_2_out_3, H0, H01, H1, H3,
       not_1_out, not_2_out, not_3_out, not_4_out, not_5_out, not_6_out, not_7_out, not_8_out;
  wire [1:0] C, H, multiplexer_1_out, multiplexer_2_out, multiplexer_3_out, multiplexer_4_out,
       multiplexer_5_out, multiplexer_6_out, multiplexer_7_out, multiplexer_8_out, or_1_out;

  Comparator #(.Bits(2)) comparator_1 (.a(C), .b(2'b10), .eq(C01));  // open: gt, lt
  Comparator #(.Bits(2)) comparator_2 (.a(H), .b(2'b10), .eq(H01));  // open: gt, lt
  and and_1 (and_1_out, not_1_out, not_2_out, c0_t);
  not not_1 (not_1_out, Warning);
  not not_2 (not_2_out, Car);
  and and_2 (and_2_out, not_3_out, Human, not_4_out);
  not not_3 (not_3_out, Warning);
  not not_4 (not_4_out, Car);
  and and_3 (and_3_out, not_5_out, not_6_out, c1_t);
  not not_5 (not_5_out, Warning);
  not not_6 (not_6_out, Human);
  and and_4 (and_4_out, not_7_out, not_8_out, Car);
  not not_7 (not_7_out, Warning);
  not not_8 (not_8_out, Human);
  Comparator #(.Bits(2)) comparator_3 (.a(C), .b(2'b00), .eq(C0));  // open: gt, lt
  Comparator #(.Bits(2)) comparator_4 (.a(H), .b(2'b00), .eq(H0));  // open: gt, lt
  or or_1 (or_1_out[0], and_1_out, and_2_out);
  or or_2 (or_1_out[1], and_3_out, and_4_out);
  Comparator #(.Bits(2)) comparator_5 (.a(C), .b(2'b01), .eq(C1));  // open: gt, lt
  Comparator #(.Bits(2)) comparator_6 (.a(H), .b(2'b01), .eq(H1));  // open: gt, lt
  Multiplexer #(.Bits(2)) multiplexer_1 (.sel(H01), .in_0(H), .in_1(2'b11), .out(multiplexer_1_out));
  Multiplexer #(.Bits(2)) multiplexer_2 (.sel(H3), .in_0(multiplexer_1_out), .in_1(2'b01), .out(multiplexer_2_out));
  Multiplexer #(.Bits(2)) multiplexer_3 (.sel(C01), .in_0(C), .in_1(2'b11), .out(multiplexer_3_out));
  Multiplexer #(.Bits(2)) multiplexer_4 (.sel(C3), .in_0(multiplexer_3_out), .in_1(2'b01), .out(multiplexer_4_out));
  D_FF #(.Bits(2)) d_ff_1 (.D(or_1_out), .C(clk), .Q({c1_t, c0_t}));  // open: nQ
  Comparator #(.Bits(2)) comparator_7 (.a(C), .b(2'b11), .eq(C3));  // open: gt, lt
  Comparator #(.Bits(2)) comparator_8 (.a(H), .b(2'b11), .eq(H3));  // open: gt, lt
  Multiplexer #(.Bits(2)) multiplexer_5 (.sel(H0), .in_0(2'b00), .in_1(2'b11), .out(multiplexer_5_out));
  Multiplexer #(.Bits(2)) multiplexer_6 (.sel(C0), .in_0(2'b00), .in_1(2'b11), .out(multiplexer_6_out));
  Multiplexer #(.Bits(2), .Selector_Bits(2)) multiplexer_7 (
    .sel({c1_t, c0_t}), .in_0(multiplexer_5_out), .in_1(2'b10), .in_2(multiplexer_2_out), .in_3(H),
    .out(multiplexer_7_out));
  Multiplexer #(.Selector_Bits(2), .Bits(2)) multiplexer_8 (
    .sel({c1_t, c0_t}), .in_0(multiplexer_6_out), .in_1(multiplexer_4_out), .in_2(2'b10), .in_3(C),
    .out(multiplexer_8_out));
  Decoder #(.Selector_Bits(2)) decoder_1 (
    .sel(H), .out_1(decoder_1_out_1), .out_2(decoder_1_out_2), .out_3(decoder_1_out_3));  // open: out_0
  D_FF #(.Bits(2)) u_H (.D(multiplexer_7_out), .C(clk), .Q(H));  // open: nQ
  D_FF #(.Bits(2)) u_C (.D(multiplexer_8_out), .C(clk), .Q(C));  // open: nQ
  LED RH (.in(decoder_1_out_1));
  LED YH (.in(decoder_1_out_3));
  LED GH (.in(decoder_1_out_2));
  Decoder #(.Selector_Bits(2)) decoder_2 (
    .sel(C), .out_1(decoder_2_out_1), .out_2(decoder_2_out_2), .out_3(decoder_2_out_3));  // open: out_0
  LED RC (.in(decoder_2_out_1));
  LED YC (.in(decoder_2_out_3));
  LED GC (.in(decoder_2_out_2));

  // Other names for the same wires on the sheet: Control[1:0] = {c1_t, c0_t}; x = Warning; y = Human; z = Car
endmodule
