// Digital circuit 2559_1.dig as structural Verilog
module _2559_1 (
  input  Start,
  input  clk,
  output [3:0] Output
);

  wire comparator_1_eq;
  wire [3:0] add_1_s, multiplexer_1_out;

  Add #(.Bits(4)) add_1 (.a(Output), .b(4'b0011), .c_i(comparator_1_eq), .s(add_1_s));  // open: c_o
  Multiplexer #(.Bits(4)) multiplexer_1 (.sel(Start), .in_0(Output), .in_1(add_1_s), .out(multiplexer_1_out));
  D_FF #(.Bits(4), .Default(2)) d_ff_1 (.D(multiplexer_1_out), .C(clk), .Q(Output));  // open: nQ
  Comparator #(.Bits(4)) comparator_1 (.a(Output), .b(4'b1110), .eq(comparator_1_eq));  // open: gt, lt
endmodule
