// Digital circuit 2563_1.dig as structural Verilog
module _2563_1 (
  input  clk,
  input  [7:0] A,
  input  [7:0] B,
  input  \input ,
  output busy,
  output [7:0] Output
);

  wire L_q, multiplexer_1_out, multiplexer_2_out, Z_q;
  wire [1:0] comparator_1_eq;
  wire [7:0] A_B, A_t, B_A, B_t, multiplexer_3_out, multiplexer_4_out, multiplexer_5_out;

  Multiplexer multiplexer_1 (.sel(L_q), .in_0(\input ), .in_1(1'b0), .out(multiplexer_1_out));
  Multiplexer multiplexer_2 (.sel(Z_q), .in_0(\input ), .in_1(L_q), .out(multiplexer_2_out));
  D_FF L (.D(multiplexer_2_out), .C(clk), .Q(L_q));  // open: nQ
  D_FF Z (.D(multiplexer_1_out), .C(clk), .Q(Z_q));  // open: nQ
  Sub #(.Bits(8)) sub_1 (.a(A_t), .b(B_t), .c_i(1'b0), .s(A_B));  // open: c_o
  Multiplexer #(.Bits(8)) multiplexer_3 (.sel(Z_q), .in_0(multiplexer_5_out), .in_1(A), .out(multiplexer_3_out));
  Multiplexer #(.Bits(8)) multiplexer_4 (.sel(Z_q), .in_0(Output), .in_1(B), .out(multiplexer_4_out));
  D_FF #(.Bits(8)) u_A (.D(multiplexer_3_out), .C(clk), .Q(A_t));  // open: nQ
  D_FF #(.Bits(8)) u_B (.D(multiplexer_4_out), .C(clk), .Q(B_t));  // open: nQ
  Sub #(.Bits(8)) sub_2 (.a(B_t), .b(A_t), .c_i(1'b0), .s(B_A));  // open: c_o
  Comparator #(.Bits(8)) comparator_1 (.a(A_t), .b(B_t), .gt(comparator_1_eq[0]), .eq(comparator_1_eq[1]));  // open: lt
  Multiplexer #(.Selector_Bits(2), .Bits(8)) multiplexer_5 (
    .sel(comparator_1_eq), .in_0(A_t), .in_1(A_B), .in_2(A_t), .in_3(A_t), .out(multiplexer_5_out));
  Multiplexer #(.Selector_Bits(2), .Bits(8)) multiplexer_6 (
    .sel(comparator_1_eq), .in_0(B_A), .in_1(B_t), .in_2(B_t), .in_3(B_t), .out(Output));
  not not_1 (busy, comparator_1_eq[1]);
endmodule
