// Digital circuit 01.dig as structural Verilog
module _01 (
  input  reset,
  input  clk,
  output A,
  output B,
  output C
);

  wire and_1_out, and_2_out, and_3_out, and_4_out, and_5_out, and_6_out, and_7_out, or_1_out, or_2_out,
       xnor_1_out;

  and and_1 (and_1_out, or_1_out, ~reset);  // And
  or or_1 (or_1_out, and_2_out, and_3_out);
  and and_2 (and_2_out, C, A);
  D_FF d_ff_1 (.D(and_1_out), .C(clk), .Q(C));  // open: nQ
  and and_3 (and_3_out, ~A, B);  // And
  and and_4 (and_4_out, ~C, A);  // And
  and and_5 (and_5_out, or_2_out, ~reset);  // And
  or or_2 (or_2_out, and_4_out, and_6_out);
  and and_6 (and_6_out, ~A, B);  // And
  D_FF d_ff_2 (.D(and_5_out), .C(clk), .Q(B));  // open: nQ
  and and_7 (and_7_out, xnor_1_out, ~reset);  // And
  xnor xnor_1 (xnor_1_out, C, B);
  D_FF d_ff_3 (.D(and_7_out), .C(clk), .Q(A));  // open: nQ

  // Notes on the sheet:
  //   clk: Hz: 2
endmodule

/* Test case TestCase:
clk reset C B A
0 0 0 0 0 
0 1 0 0 0
1 1 0 0 0
0 0 0 0 0
1 0 0 0 1
0 0 0 0 1
1 0 0 1 1
0 0 0 1 1
1 0 0 1 0
0 0 0 1 0
1 0 1 1 0
0 0 1 1 0
1 0 1 1 1
0 0 1 1 1
1 0 1 0 1
0 0 1 0 1
1 0 1 0 0
0 0 1 0 0
1 0 0 0 0
0 0 0 0 0
1 0 0 0 1
0 0 0 0 1
1 0 0 1 1
0 0 0 1 1
1 0 0 1 0
0 0 0 1 0
1 0 1 1 0
0 0 1 1 0
1 0 1 1 1
0 0 1 1 1
1 0 1 0 1
0 0 1 0 1
1 0 1 0 0
0 0 1 0 0
*/
