// Digital circuit 02.dig as structural Verilog
module _02 (
  input  [15:0] A,
  input  \input ,
  input  clk,
  output [7:0] sqrt,
  output busy,
  output [7:0] out_6,
  output out_7,
  output out_8,
  output out_9
);

  wire and_1_out, comparator_1_eq, comparator_2_eq, comparator_3_eq, comparator_4_eq, decoder_1_out_0,
       decoder_1_out_1, decoder_1_out_3, decoder_2_out_1, decoder_2_out_2, decoder_2_out_3, Load,
       multiplexer_1_out, multiplexer_2_out, multiplexer_3_out, MxM_gt_A, or_1_out, or_3_out;
  wire [7:0] add_1_s, multiplexer_4_out, multiplexer_5_out, sub_1_s;
  wire [15:0] mul_1_mul;

  Comparator #(.Bits(8)) comparator_1 (.a(out_6), .b({8{1'b1}}), .eq(comparator_1_eq));  // open: gt, lt
  Comparator #(.Bits(8)) comparator_2 (.a(out_6), .b({8{1'b1}}), .eq(comparator_2_eq));  // open: gt, lt
  and and_1 (and_1_out, ~MxM_gt_A, ~comparator_1_eq);  // And
  or or_1 (or_1_out, MxM_gt_A, comparator_2_eq);
  Multiplexer #(.Selector_Bits(3)) multiplexer_1 (
    .sel({out_7, out_8, out_9}), .in_0(1'b0), .in_1(1'b0), .in_2(or_1_out), .in_3(1'b0), .in_4(\input ),
    .in_5(1'b0), .in_6(1'b0), .in_7(1'b0), .out(multiplexer_1_out));
  Multiplexer #(.Selector_Bits(3)) multiplexer_2 (
    .sel({out_7, out_8, out_9}), .in_0(1'b0), .in_1(1'b1), .in_2(and_1_out), .in_3(1'b1), .in_4(1'b0),
    .in_5(1'b0), .in_6(1'b0), .in_7(1'b0), .out(multiplexer_2_out));
  Multiplexer #(.Selector_Bits(3)) multiplexer_3 (
    .sel({out_7, out_8, out_9}), .in_0(\input ), .in_1(1'b0), .in_2(and_1_out), .in_3(1'b0), .in_4(1'b0),
    .in_5(1'b0), .in_6(1'b0), .in_7(1'b0), .out(multiplexer_3_out));
  D_FF S1_plus (.D(multiplexer_1_out), .C(clk), .Q(out_7));  // open: nQ
  D_FF S2_plus (.D(multiplexer_2_out), .C(clk), .Q(out_8));  // open: nQ
  D_FF S3_plus (.D(multiplexer_3_out), .C(clk), .Q(out_9));  // open: nQ
  Add #(.Bits(8)) add_1 (.a(out_6), .b(8'h1), .c_i(1'b0), .s(add_1_s));  // open: c_o
  Decoder #(.Selector_Bits(3)) decoder_1 (
    .sel({out_7, out_8, out_9}), .out_0(decoder_1_out_0), .out_1(decoder_1_out_1), .out_3(decoder_1_out_3));  // open: out_2, out_4, out_5, out_6, out_7
  Comparator #(.Bits(8)) comparator_3 (.a(out_6), .b({8{1'b0}}), .eq(comparator_3_eq));  // open: gt, lt
  Comparator #(.Bits(8)) comparator_4 (.a(out_6), .b({8{1'b1}}), .eq(comparator_4_eq));  // open: gt, lt
  or or_2 (Load, decoder_1_out_0, decoder_1_out_1, decoder_1_out_3);
  or or_3 (or_3_out, comparator_3_eq, comparator_4_eq);
  Multiplexer #(.Selector_Bits(3), .Bits(8)) multiplexer_4 (
    .sel({out_7, out_8, out_9}), .in_0(out_6), .in_1({8{1'b0}}), .in_2({8{1'b0}}), .in_3(add_1_s),
    .in_4({8{1'b0}}), .in_5({8{1'b0}}), .in_6({8{1'b0}}), .in_7({8{1'b0}}), .out(multiplexer_4_out));
  Decoder #(.Selector_Bits(3)) decoder_2 (
    .sel({out_7, out_8, out_9}), .out_1(decoder_2_out_1), .out_2(decoder_2_out_2), .out_3(decoder_2_out_3));  // open: out_0, out_4, out_5, out_6, out_7
  Multiplexer #(.Bits(8)) multiplexer_5 (.sel(or_3_out), .in_0(8'h1), .in_1({8{1'b0}}), .out(multiplexer_5_out));
  Mul #(.Bits(8)) mul_1 (.a(out_6), .b(out_6), .mul(mul_1_mul));
  Register #(.Bits(8)) register_1 (.D(multiplexer_4_out), .C(clk), .en(Load), .Q(out_6));
  Comparator #(.Bits(16)) comparator_5 (.a(mul_1_mul), .b(A), .gt(MxM_gt_A));  // open: eq, lt
  or or_4 (busy, decoder_2_out_1, decoder_2_out_2, decoder_2_out_3);
  Sub #(.Bits(8)) sub_1 (.a(out_6), .b(multiplexer_5_out), .c_i(1'b0), .s(sub_1_s));  // open: c_o
  Multiplexer #(.Bits(8)) multiplexer_6 (.sel(busy), .in_0(sub_1_s), .in_1({8{1'b0}}), .out(sqrt));

  // Other names for the same wires on the sheet: M[7:0] = out_6; state[2:0] = {out_7, out_8, out_9}

  // Notes on the sheet:
  //   clk: Hz: 200
endmodule

/* Test case TestCase1:
clk A input sqrt busy
0 0 0 0 0
1 0 0 0 0
0 0 0 0 0
1 0 0 0 0
0 0 1 X X
1 0 1 X X
loop(x,1000)
0 0 0 X X
1 0 0 X X
end loop
0 0 0 0 0
1 0 0 0 0
*/

/* Test case TestCase2:
clk A input sqrt busy
0 0 0 0 0
1 0 0 0 0
0 0 0 0 0
1 0 0 0 0
0 1 1 X X
1 1 1 X X
loop(x,1000)
0 1 0 X X
1 1 0 X X
end loop
0 0 0 1 0
1 0 0 1 0
*/

/* Test case TestCase3:
clk A input sqrt busy
0 0 0 0 0
1 0 0 0 0
0 0 0 0 0
1 0 0 0 0
0 4 1 X X
1 4 1 X X
loop(x,1000)
0 4 0 X X
1 4 0 X X
end loop
0 0 0 2 0
1 0 0 2 0
*/

/* Test case TestCase4:
clk A input sqrt busy
0 0 0 0 0
1 0 0 0 0
0 0 0 0 0
1 0 0 0 0
0 9 1 X X
1 9 1 X X
loop(x,1000)
0 9 0 X X
1 9 0 X X
end loop
0 0 0 3 0
1 0 0 3 0
*/

/* Test case TestCase5:
clk A input sqrt busy
0 0 0 0 0
1 0 0 0 0
0 0 0 0 0
1 0 0 0 0
0 8 1 X X
1 8 1 X X
loop(x,1000)
0 8 0 X X
1 8 0 X X
end loop
0 0 0 2 0
1 0 0 2 0
*/
