// Digital circuit template_02.dig as structural Verilog
module template_02 (
  input  clk,
  input  \input ,
  input  [15:0] A,
  output busy,
  output [7:0] sqrt
);

  wire comparator_1_lt, L_q, multiplexer_1_out, multiplexer_2_out, Z_q;
  wire [7:0] add_1_s, add_2_s;
  wire [15:0] A_q, mul_1_mul, multiplexer_3_out;

  Multiplexer multiplexer_1 (.sel(Z_q), .in_0(\input ), .in_1(L_q), .out(multiplexer_1_out));
  Multiplexer multiplexer_2 (.sel(L_q), .in_0(\input ), .in_1(1'b0), .out(multiplexer_2_out));
  D_FF L (.D(multiplexer_1_out), .C(clk), .Q(L_q));  // open: nQ
  D_FF Z (.D(multiplexer_2_out), .C(clk), .Q(Z_q));  // open: nQ
  Multiplexer #(.Bits(16)) multiplexer_3 (.sel(Z_q), .in_0(A_q), .in_1(A), .out(multiplexer_3_out));
  D_FF #(.Bits(16)) u_A (.D(multiplexer_3_out), .C(clk), .Q(A_q));  // open: nQ
  Add #(.Bits(8)) add_1 (.a(sqrt), .b({8{1'b0}}), .c_i(busy), .s(add_1_s));  // open: c_o
  D_FF_AS #(.Bits(8)) u_sqrt (.Set(1'b0), .D(add_1_s), .C(clk), .Clr(Z_q), .Q(sqrt));  // open: nQ
  Add #(.Bits(8)) add_2 (.a(sqrt), .b({8{1'b0}}), .c_i(1'b1), .s(add_2_s));  // open: c_o
  Mul #(.Bits(8)) mul_1 (.a(add_2_s), .b(add_2_s), .mul(mul_1_mul));
  Comparator #(.Bits(16)) comparator_1 (.a(A_q), .b(mul_1_mul), .lt(comparator_1_lt));  // open: gt, eq
  not not_1 (busy, comparator_1_lt);
endmodule

/* Test case TestCase1:
clk A input sqrt busy
0 0 0 0 0
1 0 0 0 0
0 0 0 0 0
1 0 0 0 0
0 0 1 X X
1 0 1 X X
loop(x,1000)
0 0 0 X X
1 0 0 X X
end loop
0 0 0 0 0
1 0 0 0 0
*/

/* Test case TestCase2:
clk A input sqrt busy
0 0 0 0 0
1 0 0 0 0
0 0 0 0 0
1 0 0 0 0
0 1 1 X X
1 1 1 X X
loop(x,1000)
0 1 0 X X
1 1 0 X X
end loop
0 0 0 1 0
1 0 0 1 0
*/

/* Test case TestCase3:
clk A input sqrt busy
0 0 0 0 0
1 0 0 0 0
0 0 0 0 0
1 0 0 0 0
0 4 1 X X
1 4 1 X X
loop(x,1000)
0 4 0 X X
1 4 0 X X
end loop
0 0 0 2 0
1 0 0 2 0
*/

/* Test case TestCase4:
clk A input sqrt busy
0 0 0 0 0
1 0 0 0 0
0 0 0 0 0
1 0 0 0 0
0 9 1 X X
1 9 1 X X
loop(x,1000)
0 9 0 X X
1 9 0 X X
end loop
0 0 0 3 0
1 0 0 3 0
*/

/* Test case TestCase5:
clk A input sqrt busy
0 0 0 0 0
1 0 0 0 0
0 0 0 0 0
1 0 0 0 0
0 8 1 X X
1 8 1 X X
loop(x,1000)
0 8 0 X X
1 8 0 X X
end loop
0 0 0 2 0
1 0 0 2 0
*/
