// Digital circuit n_square.dig as structural Verilog
module n_square (
  input  clk,
  input  [7:0] n,
  output [7:0] cnt,
  output [15:0] y
);

  wire comparator_1_gt, comparator_2_gt, multiplexer_6_out, ready;
  wire [1:0] d_ff_1_q, multiplexer_1_out, multiplexer_2_out, state;
  wire [7:0] add_1_s, multiplexer_4_out;
  wire [15:0] add_2_s, bitextender_1_out, multiplexer_5_out;

  Comparator #(.Bits(8)) comparator_1 (.a(n), .b({8{1'b0}}), .gt(comparator_1_gt));  // open: eq, lt
  Comparator #(.Bits(8)) comparator_2 (.a(cnt), .b(n), .gt(comparator_2_gt));  // open: eq, lt
  Multiplexer #(.Bits(2)) multiplexer_1 (.sel(comparator_1_gt), .in_0(2'b00), .in_1(2'b01), .out(multiplexer_1_out));
  Multiplexer #(.Bits(2)) multiplexer_2 (.sel(comparator_2_gt), .in_0(2'b01), .in_1(2'b10), .out(multiplexer_2_out));
  Multiplexer #(.Selector_Bits(2), .Bits(2)) multiplexer_3 (
    .sel(d_ff_1_q), .in_0(multiplexer_1_out), .in_1(multiplexer_2_out), .in_2(2'b10), .in_3(2'b11),
    .out(state));
  D_FF #(.Bits(2)) d_ff_1 (.D(state), .C(clk), .Q(d_ff_1_q));  // open: nQ
  Add #(.Bits(8)) add_1 (.a(cnt), .b({8{1'b0}}), .c_i(1'b1), .s(add_1_s));  // open: c_o
  BitExtender bitextender_1 (.in(n), .out(bitextender_1_out));
  Add #(.Bits(16)) add_2 (.a(y), .b(bitextender_1_out), .c_i(1'b0), .s(add_2_s));  // open: c_o
  Multiplexer #(.Selector_Bits(2), .Bits(8)) multiplexer_4 (
    .sel(state), .in_0(8'h1), .in_1(add_1_s), .in_2(cnt), .in_3(cnt), .out(multiplexer_4_out));
  Multiplexer #(.Selector_Bits(2), .Bits(16)) multiplexer_5 (
    .sel(state), .in_0({16{1'b0}}), .in_1(add_2_s), .in_2(y), .in_3(y), .out(multiplexer_5_out));
  Multiplexer #(.Selector_Bits(2)) multiplexer_6 (
    .sel(state), .in_0(1'b0), .in_1(ready), .in_2(ready), .in_3(1'b1), .out(multiplexer_6_out));
  D_FF #(.Bits(8)) d_ff_2 (.D(multiplexer_4_out), .C(clk), .Q(cnt));  // open: nQ
  D_FF #(.Bits(16)) d_ff_3 (.D(multiplexer_5_out), .C(clk), .Q(y));  // open: nQ
  D_FF d_ff_4 (.D(multiplexer_6_out), .C(clk), .Q(ready));  // open: nQ

  // Notes on the sheet:
  //   clk: Hz: 100
endmodule
