// Digital circuit 64_01.dig as structural Verilog
module _64_01 (
  input  [2:0] in_1,
  input  [2:0] in_2
);

  wire a, comparator_1_gt;
  wire [2:0] add_1_s;
  wire [3:3] add_1_c_o;

  Add #(.Bits(3)) add_1 (.a(in_1), .b(in_2), .c_i(1'b0), .s(add_1_s), .c_o(add_1_c_o[3]));
  Comparator #(.Bits(4)) comparator_1 (.a({add_1_c_o[3], add_1_s}), .b(4'b0010), .gt(comparator_1_gt));  // open: eq, lt
  not not_1 (a, comparator_1_gt);
  Seven_Seg seven_seg_1 (.a(a), .b(1'b1), .c(1'b1), .d(a), .e(a), .f(a), .g(1'b0), .dp(1'b0));

  // Other names for the same wires on the sheet: d = a; e = a; f = a
endmodule
